// Logisim project DIGITAL SYSTEM LAB.circ as structural Verilog
module understanding_logisim (
  input  A,
  input  B,
  input  C,
  input  D,
  output A_prime_B_B_prime_C_C_prime_D
);

  wire and_using_nand_1_s, and_using_nand_2_s, and_using_nand_3_s, not_using_nand_1_a_prime,
       not_using_nand_2_a_prime, not_using_nand_3_a_prime, or_using_nand_1_s;

  not_using_nand not_using_nand_1 (.A(A), .A_prime(not_using_nand_1_a_prime));
  not_using_nand not_using_nand_2 (.A(B), .A_prime(not_using_nand_2_a_prime));
  not_using_nand not_using_nand_3 (.A(C), .A_prime(not_using_nand_3_a_prime));
  and_using_nand and_using_nand_1 (.A(not_using_nand_1_a_prime), .B(B), .S(and_using_nand_1_s));
  and_using_nand and_using_nand_2 (.A(not_using_nand_2_a_prime), .B(C), .S(and_using_nand_2_s));
  and_using_nand and_using_nand_3 (.A(not_using_nand_3_a_prime), .B(D), .S(and_using_nand_3_s));
  or_using_nand or_using_nand_1 (.A(and_using_nand_1_s), .B(and_using_nand_2_s), .S(or_using_nand_1_s));
  or_using_nand or_using_nand_2 (.A(or_using_nand_1_s), .B(and_using_nand_3_s), .S(A_prime_B_B_prime_C_C_prime_D));

  // Notes on the sheet:
  //   A'B
  //   B'C
  //   COMBINATORIAL CIRCUIT USING LOGISIM
  //   A'B+B'C
  //   C'D
endmodule

// AND
module and_using_nand (
  input  A,
  input  B,
  output S
);

  wire nand_1_out;

  nand nand_1 (nand_1_out, A, B);
  nand nand_2 (S, nand_1_out, nand_1_out);

  // Notes on the sheet:
  //   AND USING NAND
endmodule

// OR
module or_using_nand (
  input  A,
  input  B,
  output S
);

  wire nand_1_out, nand_2_out;

  nand nand_1 (nand_1_out, A, A);
  nand nand_2 (nand_2_out, B, B);
  nand nand_3 (S, nand_1_out, nand_2_out);

  // Notes on the sheet:
  //   OR USING NAND
endmodule

// NOT
module not_using_nand (
  input  A,
  output A_prime
);

  nand nand_1 (A_prime, A, A);

  // Notes on the sheet:
  //   NOT USING NAND
endmodule

// XOR
module xor_using_nand (
  input  A,
  input  B,
  output S
);

  wire nand_1_out, nand_2_out, nand_3_out;

  nand nand_1 (nand_1_out, A, B);
  nand nand_2 (nand_2_out, A, nand_1_out);
  nand nand_3 (nand_3_out, nand_1_out, B);
  nand nand_4 (S, nand_2_out, nand_3_out);

  // Notes on the sheet:
  //   XOR USING NAND
endmodule

module _4x1_MUX (
  input  S0,
  input  S1,
  input  I3,
  input  I2,
  input  I1,
  input  I0,
  output out_7
);

  wire and_using_nand_1_s, and_using_nand_2_s, and_using_nand_3_s, and_using_nand_4_s, and_using_nand_5_s,
       and_using_nand_6_s, and_using_nand_7_s, and_using_nand_8_s, not_using_nand_1_a_prime,
       not_using_nand_2_a_prime, or_using_nand_1_s, or_using_nand_2_s;

  not_using_nand not_using_nand_1 (.A(S0), .A_prime(not_using_nand_1_a_prime));
  not_using_nand not_using_nand_2 (.A(S1), .A_prime(not_using_nand_2_a_prime));
  and_using_nand and_using_nand_1 (.A(not_using_nand_1_a_prime), .B(not_using_nand_2_a_prime), .S(and_using_nand_1_s));
  and_using_nand and_using_nand_2 (.A(and_using_nand_1_s), .B(I0), .S(and_using_nand_2_s));
  and_using_nand and_using_nand_3 (.A(not_using_nand_1_a_prime), .B(S1), .S(and_using_nand_3_s));
  and_using_nand and_using_nand_4 (.A(and_using_nand_3_s), .B(I1), .S(and_using_nand_4_s));
  and_using_nand and_using_nand_5 (.A(S0), .B(not_using_nand_2_a_prime), .S(and_using_nand_5_s));
  and_using_nand and_using_nand_6 (.A(and_using_nand_5_s), .B(I2), .S(and_using_nand_6_s));
  and_using_nand and_using_nand_7 (.A(S0), .B(S1), .S(and_using_nand_7_s));
  and_using_nand and_using_nand_8 (.A(and_using_nand_7_s), .B(I3), .S(and_using_nand_8_s));
  or_using_nand or_using_nand_1 (.A(and_using_nand_2_s), .B(and_using_nand_4_s), .S(or_using_nand_1_s));
  or_using_nand or_using_nand_2 (.A(and_using_nand_6_s), .B(and_using_nand_8_s), .S(or_using_nand_2_s));
  or_using_nand or_using_nand_3 (.A(or_using_nand_1_s), .B(or_using_nand_2_s), .S(out_7));
endmodule

module _1x4_DEMUX (
  input  S0,
  input  S1,
  input  INPUT,
  input  ENABLE,
  output Y0,
  output Y1,
  output Y2,
  output Y3
);

  wire and_using_nand_1_s, and_using_nand_2_s, and_using_nand_3_s, and_using_nand_4_s, and_using_nand_5_s,
       and_using_nand_7_s, and_using_nand_10_s, and_using_nand_11_s, not_using_nand_1_a_prime,
       not_using_nand_2_a_prime;

  not_using_nand not_using_nand_1 (.A(S0), .A_prime(not_using_nand_1_a_prime));
  not_using_nand not_using_nand_2 (.A(S1), .A_prime(not_using_nand_2_a_prime));
  and_using_nand and_using_nand_1 (.A(not_using_nand_1_a_prime), .B(not_using_nand_2_a_prime), .S(and_using_nand_1_s));
  and_using_nand and_using_nand_2 (.A(not_using_nand_1_a_prime), .B(S1), .S(and_using_nand_2_s));
  and_using_nand and_using_nand_3 (.A(not_using_nand_2_a_prime), .B(S0), .S(and_using_nand_3_s));
  and_using_nand and_using_nand_4 (.A(S1), .B(S0), .S(and_using_nand_4_s));
  and_using_nand and_using_nand_5 (.A(and_using_nand_1_s), .B(ENABLE), .S(and_using_nand_5_s));
  and_using_nand and_using_nand_6 (.A(and_using_nand_5_s), .B(INPUT), .S(Y0));
  and_using_nand and_using_nand_7 (.A(and_using_nand_2_s), .B(ENABLE), .S(and_using_nand_7_s));
  and_using_nand and_using_nand_8 (.A(and_using_nand_7_s), .B(INPUT), .S(Y1));
  and_using_nand and_using_nand_9 (.A(and_using_nand_10_s), .B(INPUT), .S(Y2));
  and_using_nand and_using_nand_10 (.A(and_using_nand_3_s), .B(ENABLE), .S(and_using_nand_10_s));
  and_using_nand and_using_nand_11 (.A(and_using_nand_4_s), .B(ENABLE), .S(and_using_nand_11_s));
  and_using_nand and_using_nand_12 (.A(and_using_nand_11_s), .B(INPUT), .S(Y3));
endmodule

module _2_bit_adder (
  input  A0,
  input  B0,
  input  A1,
  input  B1,
  output S0,
  output C,
  output S1
);

  wire and_using_nand_1_s, and_using_nand_2_s, and_using_nand_3_s, xor_using_nand_2_s;

  xor_using_nand xor_using_nand_1 (.A(A0), .B(B0), .S(S0));
  and_using_nand and_using_nand_1 (.A(A0), .B(B0), .S(and_using_nand_1_s));
  xor_using_nand xor_using_nand_2 (.A(A1), .B(B1), .S(xor_using_nand_2_s));
  and_using_nand and_using_nand_2 (.A(B1), .B(A1), .S(and_using_nand_2_s));
  xor_using_nand xor_using_nand_3 (.A(xor_using_nand_2_s), .B(and_using_nand_1_s), .S(S1));
  and_using_nand and_using_nand_3 (.A(and_using_nand_1_s), .B(xor_using_nand_2_s), .S(and_using_nand_3_s));
  or_using_nand or_using_nand_1 (.A(and_using_nand_3_s), .B(and_using_nand_2_s), .S(C));
endmodule

// HA
module half_adder (
  input  A,
  input  B,
  output S,
  output Co
);

  xor_using_nand xor_using_nand_1 (.A(A), .B(B), .S(S));
  and_using_nand and_using_nand_1 (.A(A), .B(B), .S(Co));

  // Notes on the sheet:
  //   HALF ADDER
endmodule

// FA
module full_adder_using_half_adder (
  input  A,
  input  B,
  input  Cin,
  output S,
  output Cout
);

  wire half_adder_1_co, half_adder_1_s, half_adder_2_co;

  half_adder half_adder_1 (.A(A), .B(B), .S(half_adder_1_s), .Co(half_adder_1_co));
  half_adder half_adder_2 (.A(half_adder_1_s), .B(Cin), .S(S), .Co(half_adder_2_co));
  or_using_nand or_using_nand_1 (.A(half_adder_2_co), .B(half_adder_1_co), .S(Cout));

  // Notes on the sheet:
  //   FULL ADDER
endmodule

module _4_bit_parallel_adder_using_FA (
  input  B3,
  input  B2,
  input  B1,
  input  B0,
  input  Cin,
  input  A3,
  input  A2,
  input  A1,
  input  A0,
  output S1,
  output S0,
  output Cout,
  output S3,
  output S2
);

  wire full_adder_using_half_adder_1_cout, full_adder_using_half_adder_2_cout,
       full_adder_using_half_adder_3_cout;

  full_adder_using_half_adder full_adder_using_half_adder_1 (
    .A(A0), .B(B0), .Cin(Cin), .S(S0), .Cout(full_adder_using_half_adder_1_cout));
  full_adder_using_half_adder full_adder_using_half_adder_2 (
    .A(A1), .B(B1), .Cin(full_adder_using_half_adder_1_cout), .S(S1),
    .Cout(full_adder_using_half_adder_2_cout));
  full_adder_using_half_adder full_adder_using_half_adder_3 (
    .A(A2), .B(B2), .Cin(full_adder_using_half_adder_2_cout), .S(S2),
    .Cout(full_adder_using_half_adder_3_cout));
  full_adder_using_half_adder full_adder_using_half_adder_4 (
    .A(A3), .B(B3), .Cin(full_adder_using_half_adder_3_cout), .S(S3), .Cout(Cout));

  // Notes on the sheet:
  //   C0
  //   C1
  //   C2
  //   C3
endmodule

module bcd_to_xs3_mux (
  input  in_1,
  input  in_2,
  input  A,
  input  [2:0] BCD,
  output E3,
  output E2,
  output E1,
  output E0
);

  wire A_prime_out;

  not A_prime (A_prime_out, A);
  Multiplexer #(.select(3), .enable("false")) multiplexer_1 (
    .in0(in_1), .in1(in_2), .in2(in_2), .in3(A_prime_out), .in4(A_prime_out), .in5(in_2), .in6(in_2),
    .in7(A_prime_out), .out(E1), .sel(BCD));
  Multiplexer #(.select(3), .enable("false")) multiplexer_2 (
    .in0(A), .in1(A), .in2(in_2), .in3(in_2), .in4(in_2), .in5(A_prime_out), .in6(A_prime_out),
    .in7(A_prime_out), .out(E3), .sel(BCD));
  Multiplexer #(.select(3), .enable("false")) multiplexer_3 (
    .in0(in_1), .in1(in_2), .in2(A_prime_out), .in3(in_2), .in4(A_prime_out), .in5(in_2), .in6(A_prime_out),
    .in7(in_2), .out(E0), .sel(BCD));
  Multiplexer #(.select(3), .enable("false")) multiplexer_4 (
    .in0(in_2), .in1(in_1), .in2(A_prime_out), .in3(A_prime_out), .in4(A_prime_out), .in5(in_2), .in6(in_2),
    .in7(in_2), .out(E2), .sel(BCD));

  // Notes on the sheet:
  //   BCD to EXCESS-3 USING MUX
endmodule

module dec_to_bin_encoder (
  input  D9,
  input  D8,
  input  D7,
  input  D6,
  input  D5,
  input  D4,
  input  D3,
  input  D2,
  input  D1,
  input  D0,
  output B3,
  output B2,
  output B1,
  output B0
);

  wire nand_1_out, nand_2_out, nand_3_out, nand_4_out, nand_5_out, nand_6_out, nand_7_out, nand_8_out,
       nand_10_out, nand_11_out, nand_12_out, nand_13_out, nand_14_out, nand_15_out, nand_16_out,
       nand_17_out, nand_18_out, nand_19_out, nand_20_out, nand_21_out, nand_22_out, nand_23_out,
       nand_24_out, nand_25_out, nand_26_out, nand_27_out, nand_28_out, nand_31_out, nand_32_out;

  nand nand_1 (nand_1_out, D9, D9);
  nand nand_2 (nand_2_out, D8, D8);
  nand nand_3 (nand_3_out, D4, D4);
  nand nand_4 (nand_4_out, D5, D5);
  nand nand_5 (nand_5_out, D3, D3);
  nand nand_6 (nand_6_out, D2, D2);
  nand nand_7 (nand_7_out, D1, D1);
  nand nand_8 (nand_8_out, D3, D3);
  nand nand_9 (B3, nand_1_out, nand_2_out);
  nand nand_10 (nand_10_out, nand_3_out, nand_4_out);
  nand nand_11 (nand_11_out, nand_5_out, nand_6_out);
  nand nand_12 (nand_12_out, nand_7_out, nand_8_out);
  nand nand_13 (nand_13_out, nand_10_out, nand_10_out);
  nand nand_14 (nand_14_out, nand_13_out, nand_15_out);
  nand nand_15 (nand_15_out, D6, D6);
  nand nand_16 (nand_16_out, nand_11_out, nand_11_out);
  nand nand_17 (nand_17_out, nand_16_out, nand_18_out);
  nand nand_18 (nand_18_out, D6, D6);
  nand nand_19 (nand_19_out, nand_12_out, nand_12_out);
  nand nand_20 (nand_20_out, nand_19_out, nand_21_out);
  nand nand_21 (nand_21_out, D5, D5);
  nand nand_22 (nand_22_out, nand_14_out, nand_14_out);
  nand nand_23 (nand_23_out, D7, D7);
  nand nand_24 (nand_24_out, nand_17_out, nand_17_out);
  nand nand_25 (nand_25_out, D7, D7);
  nand nand_26 (nand_26_out, nand_20_out, nand_20_out);
  nand nand_27 (nand_27_out, D7, D7);
  nand nand_28 (nand_28_out, nand_26_out, nand_27_out);
  nand nand_29 (B2, nand_22_out, nand_23_out);
  nand nand_30 (B1, nand_24_out, nand_25_out);
  nand nand_31 (nand_31_out, nand_28_out, nand_28_out);
  nand nand_32 (nand_32_out, D9, D9);
  nand nand_33 (B0, nand_31_out, nand_32_out);

  // Notes on the sheet:
  //   DECIMAL to BINARY Encoder
endmodule

module bin_to_dec_decoder (
  input  B3,
  input  B2,
  input  B1,
  input  B0,
  output D4,
  output D3,
  output D2,
  output D1,
  output D0,
  output D9,
  output D8,
  output D7,
  output D6,
  output D5
);

  wire nand_1_out, nand_2_out, nand_3_out, nand_4_out, nand_5_out, nand_6_out, nand_7_out, nand_8_out,
       nand_9_out, nand_10_out, nand_11_out, nand_12_out, nand_13_out, nand_14_out, nand_15_out, nand_16_out,
       nand_17_out, nand_18_out, nand_19_out, nand_20_out, nand_21_out, nand_22_out, nand_23_out,
       nand_24_out, nand_25_out, nand_26_out, nand_27_out, nand_28_out, nand_29_out, nand_30_out,
       nand_31_out, nand_32_out, nand_33_out, nand_34_out;

  nand nand_1 (nand_1_out, B3, B3);
  nand nand_2 (nand_2_out, B2, B2);
  nand nand_3 (nand_3_out, B1, B1);
  nand nand_4 (nand_4_out, B0, B0);
  nand nand_5 (nand_5_out, nand_1_out, nand_2_out);
  nand nand_6 (nand_6_out, nand_5_out, nand_5_out);
  nand nand_7 (nand_7_out, nand_1_out, nand_2_out);
  nand nand_8 (nand_8_out, nand_7_out, nand_7_out);
  nand nand_9 (nand_9_out, nand_2_out, B1);
  nand nand_10 (nand_10_out, nand_2_out, B1);
  nand nand_11 (nand_11_out, B2, nand_3_out);
  nand nand_12 (nand_12_out, B2, nand_3_out);
  nand nand_13 (nand_13_out, B2, B1);
  nand nand_14 (nand_14_out, B2, B1);
  nand nand_15 (nand_15_out, B3, nand_4_out);
  nand nand_16 (nand_16_out, B3, B0);
  nand nand_17 (nand_17_out, nand_6_out, nand_3_out);
  nand nand_18 (nand_18_out, nand_8_out, nand_3_out);
  nand nand_19 (nand_19_out, nand_9_out, nand_9_out);
  nand nand_20 (nand_20_out, nand_10_out, nand_10_out);
  nand nand_21 (nand_21_out, nand_11_out, nand_11_out);
  nand nand_22 (nand_22_out, nand_12_out, nand_12_out);
  nand nand_23 (nand_23_out, nand_13_out, nand_13_out);
  nand nand_24 (nand_24_out, nand_14_out, nand_14_out);
  nand nand_25 (nand_25_out, nand_17_out, nand_17_out);
  nand nand_26 (nand_26_out, nand_25_out, nand_4_out);
  nand nand_27 (nand_27_out, nand_18_out, nand_18_out);
  nand nand_28 (nand_28_out, nand_27_out, B0);
  nand nand_29 (nand_29_out, nand_19_out, nand_4_out);
  nand nand_30 (nand_30_out, nand_20_out, B0);
  nand nand_31 (nand_31_out, nand_21_out, nand_4_out);
  nand nand_32 (nand_32_out, nand_22_out, B0);
  nand nand_33 (nand_33_out, nand_23_out, nand_4_out);
  nand nand_34 (nand_34_out, nand_24_out, B0);
  nand nand_35 (D0, nand_26_out, nand_26_out);
  nand nand_36 (D1, nand_28_out, nand_28_out);
  nand nand_37 (D2, nand_29_out, nand_29_out);
  nand nand_38 (D3, nand_30_out, nand_30_out);
  nand nand_39 (D4, nand_31_out, nand_31_out);
  nand nand_40 (D5, nand_32_out, nand_32_out);
  nand nand_41 (D6, nand_33_out, nand_33_out);
  nand nand_42 (D7, nand_34_out, nand_34_out);
  nand nand_43 (D8, nand_15_out, nand_15_out);
  nand nand_44 (D9, nand_16_out, nand_16_out);

  // Notes on the sheet:
  //   BINARY to DECIMAL Decoder
endmodule

module _3_bit_comparator__bts (
  input  A,
  input  B,
  output A_B,
  output A_B_2,
  output A_B_3
);

  wire not_using_nand_1_a_prime, not_using_nand_2_a_prime, or_using_nand_1_s;

  not_using_nand not_using_nand_1 (.A(A), .A_prime(not_using_nand_1_a_prime));
  not_using_nand not_using_nand_2 (.A(B), .A_prime(not_using_nand_2_a_prime));
  and_using_nand and_using_nand_1 (.A(not_using_nand_1_a_prime), .B(B), .S(A_B));
  and_using_nand and_using_nand_2 (.A(A), .B(not_using_nand_2_a_prime), .S(A_B_3));
  or_using_nand or_using_nand_1 (.A(A_B), .B(A_B_3), .S(or_using_nand_1_s));
  not_using_nand not_using_nand_3 (.A(or_using_nand_1_s), .A_prime(A_B_2));
endmodule

module _3_bit_comparator (
  input  A2,
  input  A1,
  input  A0,
  input  B2,
  input  B1,
  input  B0,
  output A_B,
  output A_B_2,
  output A_B_3
);

  wire and_using_nand_1_s, and_using_nand_2_s, and_using_nand_3_s, and_using_nand_4_s, and_using_nand_5_s,
       and_using_nand_6_s, and_using_nand_7_s, n3_bit_comparator_bts_1_a_b, n3_bit_comparator_bts_1_a_b_2,
       n3_bit_comparator_bts_1_a_b_3, n3_bit_comparator_bts_2_a_b, n3_bit_comparator_bts_2_a_b_2,
       n3_bit_comparator_bts_2_a_b_3, n3_bit_comparator_bts_3_a_b, n3_bit_comparator_bts_3_a_b_2,
       n3_bit_comparator_bts_3_a_b_3, or_using_nand_1_s, or_using_nand_2_s;

  _3_bit_comparator__bts u_3_bit_comparator_bts_1 (
    .A(A2), .B(B2), .A_B(n3_bit_comparator_bts_1_a_b), .A_B_2(n3_bit_comparator_bts_1_a_b_2),
    .A_B_3(n3_bit_comparator_bts_1_a_b_3));
  _3_bit_comparator__bts u_3_bit_comparator_bts_2 (
    .A(A1), .B(B1), .A_B(n3_bit_comparator_bts_2_a_b), .A_B_2(n3_bit_comparator_bts_2_a_b_2),
    .A_B_3(n3_bit_comparator_bts_2_a_b_3));
  _3_bit_comparator__bts u_3_bit_comparator_bts_3 (
    .A(A0), .B(B0), .A_B(n3_bit_comparator_bts_3_a_b), .A_B_2(n3_bit_comparator_bts_3_a_b_2),
    .A_B_3(n3_bit_comparator_bts_3_a_b_3));
  and_using_nand and_using_nand_1 (
    .A(n3_bit_comparator_bts_1_a_b_2), .B(n3_bit_comparator_bts_2_a_b_3), .S(and_using_nand_1_s));
  and_using_nand and_using_nand_2 (
    .A(n3_bit_comparator_bts_2_a_b_2), .B(n3_bit_comparator_bts_3_a_b), .S(and_using_nand_2_s));
  and_using_nand and_using_nand_3 (
    .A(n3_bit_comparator_bts_2_a_b_2), .B(n3_bit_comparator_bts_3_a_b_3), .S(and_using_nand_3_s));
  and_using_nand and_using_nand_4 (
    .A(n3_bit_comparator_bts_1_a_b_2), .B(n3_bit_comparator_bts_2_a_b), .S(and_using_nand_4_s));
  and_using_nand and_using_nand_5 (.A(n3_bit_comparator_bts_1_a_b_2), .B(and_using_nand_2_s), .S(and_using_nand_5_s));
  and_using_nand and_using_nand_6 (.A(n3_bit_comparator_bts_1_a_b_2), .B(and_using_nand_3_s), .S(and_using_nand_6_s));
  or_using_nand or_using_nand_1 (.A(n3_bit_comparator_bts_1_a_b), .B(and_using_nand_5_s), .S(or_using_nand_1_s));
  and_using_nand and_using_nand_7 (
    .A(n3_bit_comparator_bts_2_a_b_2), .B(n3_bit_comparator_bts_3_a_b_2), .S(and_using_nand_7_s));
  or_using_nand or_using_nand_2 (.A(and_using_nand_6_s), .B(n3_bit_comparator_bts_1_a_b_3), .S(or_using_nand_2_s));
  or_using_nand or_using_nand_3 (.A(or_using_nand_1_s), .B(and_using_nand_4_s), .S(A_B));
  and_using_nand and_using_nand_8 (.A(n3_bit_comparator_bts_1_a_b_2), .B(and_using_nand_7_s), .S(A_B_2));
  or_using_nand or_using_nand_4 (.A(and_using_nand_1_s), .B(or_using_nand_2_s), .S(A_B_3));
endmodule

module CLA__bts (
  input  A,
  input  Cin,
  input  B,
  output Cout
);

  wire and_using_nand_1_s, and_using_nand_2_s, xor_using_nand_1_s;

  and_using_nand and_using_nand_1 (.A(A), .B(B), .S(and_using_nand_1_s));
  xor_using_nand xor_using_nand_1 (.A(A), .B(B), .S(xor_using_nand_1_s));
  and_using_nand and_using_nand_2 (.A(xor_using_nand_1_s), .B(Cin), .S(and_using_nand_2_s));
  or_using_nand or_using_nand_1 (.A(and_using_nand_2_s), .B(and_using_nand_1_s), .S(Cout));
endmodule

module carry_look_ahead_adder (
  input  A3,
  input  A2,
  input  A1,
  input  A0,
  input  Cin,
  input  B3,
  input  B2,
  input  B1,
  input  B0,
  output CARRY,
  output S3,
  output S2,
  output S1,
  output S0
);

  wire cla_bts_1_cout, cla_bts_2_cout, cla_bts_3_cout, xor_using_nand_1_s, xor_using_nand_3_s,
       xor_using_nand_4_s, xor_using_nand_7_s;

  CLA__bts cla_bts_1 (.A(A0), .Cin(Cin), .B(B0), .Cout(cla_bts_1_cout));
  xor_using_nand xor_using_nand_1 (.A(A0), .B(B0), .S(xor_using_nand_1_s));
  xor_using_nand xor_using_nand_2 (.A(xor_using_nand_1_s), .B(Cin), .S(S0));
  xor_using_nand xor_using_nand_3 (.A(A1), .B(B1), .S(xor_using_nand_3_s));
  CLA__bts cla_bts_2 (.A(A1), .Cin(cla_bts_1_cout), .B(B1), .Cout(cla_bts_2_cout));
  xor_using_nand xor_using_nand_4 (.A(A2), .B(B2), .S(xor_using_nand_4_s));
  xor_using_nand xor_using_nand_5 (.A(xor_using_nand_3_s), .B(cla_bts_1_cout), .S(S1));
  xor_using_nand xor_using_nand_6 (.A(xor_using_nand_4_s), .B(cla_bts_2_cout), .S(S2));
  CLA__bts cla_bts_3 (.A(A2), .Cin(cla_bts_2_cout), .B(B2), .Cout(cla_bts_3_cout));
  xor_using_nand xor_using_nand_7 (.A(A3), .B(B3), .S(xor_using_nand_7_s));
  CLA__bts cla_bts_4 (.A(A3), .Cin(cla_bts_3_cout), .B(B3), .Cout(CARRY));
  xor_using_nand xor_using_nand_8 (.A(xor_using_nand_7_s), .B(cla_bts_3_cout), .S(S3));

  // Notes on the sheet:
  //   C0
  //   C2
  //   C3
endmodule

module SR_flip_flop (
  input  S,
  input  CLK,
  input  R,
  output Q,
  output Q_prime
);

  wire nand_1_out, nand_2_out;

  nand nand_1 (nand_1_out, S, CLK);
  nand nand_2 (nand_2_out, CLK, R);
  nand nand_3 (Q, nand_1_out, Q_prime);
  nand nand_4 (Q_prime, Q, nand_2_out);
endmodule

module D_flip_flop (
  input  D,
  input  CLK,
  output Q,
  output Q_prime
);

  wire nand_1_out, nand_2_out, not_1_out;

  not not_1 (not_1_out, D);
  nand nand_1 (nand_1_out, D, CLK);
  nand nand_2 (nand_2_out, CLK, not_1_out);
  nand nand_3 (Q, nand_1_out, Q_prime);
  nand nand_4 (Q_prime, Q, nand_2_out);
endmodule

module JK_flip_flop (
  input  J,
  input  CLK,
  input  K,
  output Q,
  output Q_prime
);

  wire nand_1_out, nand_2_out, nand_3_out, nand_4_out;

  nand nand_1 (nand_1_out, J, CLK);
  nand nand_2 (nand_2_out, CLK, K);
  nand nand_3 (nand_3_out, Q_prime, nand_1_out);
  nand nand_4 (nand_4_out, nand_2_out, Q);
  nand nand_5 (Q, nand_3_out, Q_prime);
  nand nand_6 (Q_prime, Q, nand_4_out);
endmodule

module _2_bit_counter (
  input  CLK,
  output S1,
  output S0
);

  wire not_using_nand_1_a_prime, not_using_nand_2_a_prime;

  not_using_nand not_using_nand_1 (.A(CLK), .A_prime(not_using_nand_1_a_prime));
  J_K_Flip_Flop j_k_ff_1 (.J(1'b1), .clk(not_using_nand_1_a_prime), .K(1'b1), .Q(S0));  // open: Qn, preset, en, reset
  not_using_nand not_using_nand_2 (.A(S0), .A_prime(not_using_nand_2_a_prime));
  J_K_Flip_Flop j_k_ff_2 (.J(1'b1), .clk(not_using_nand_2_a_prime), .K(1'b1), .Q(S1));  // open: Qn, preset, en, reset
endmodule

module ripple_counter (
  input  CLK,
  input  CLEAR,
  output A2,
  output A1,
  output A0
);

  wire t_ff_1_qn, t_ff_2_qn;

  T_Flip_Flop #(.trigger("falling")) t_ff_1 (
    .clk(CLK), .T(1'b1), .Q(A0), .Qn(t_ff_1_qn), .reset(CLEAR));  // open: preset, en
  T_Flip_Flop #(.trigger("falling")) t_ff_2 (
    .clk(t_ff_1_qn), .T(1'b1), .Q(A1), .Qn(t_ff_2_qn), .reset(CLEAR));  // open: preset, en
  T_Flip_Flop #(.trigger("falling")) t_ff_3 (.clk(t_ff_2_qn), .T(1'b1), .Q(A2), .reset(CLEAR));  // open: Qn, preset, en

  // Notes on the sheet:
  //   RIPPLE COUNTER
endmodule

module SISO_shift (
  input  CLK,
  input  SERIAL_IN,
  output SERIAL_OUT
);

  wire d_ff_1_q, d_ff_2_q, d_ff_3_q;

  D_Flip_Flop d_ff_1 (.clk(CLK), .D(SERIAL_IN), .Q(d_ff_1_q));  // open: Qn, preset, en, reset
  D_Flip_Flop d_ff_2 (.clk(CLK), .D(d_ff_1_q), .Q(d_ff_2_q));  // open: Qn, preset, en, reset
  D_Flip_Flop d_ff_3 (.clk(CLK), .D(d_ff_2_q), .Q(d_ff_3_q));  // open: Qn, preset, en, reset
  D_Flip_Flop d_ff_4 (.clk(CLK), .D(d_ff_3_q), .Q(SERIAL_OUT));  // open: Qn, preset, en, reset

  // Notes on the sheet:
  //   REGISTER
endmodule

module SIPO_shift (
  input  CLK,
  input  SERIAL_IN,
  output A3,
  output A2,
  output A1,
  output A0
);

  D_Flip_Flop d_ff_1 (.clk(CLK), .D(SERIAL_IN), .Q(A0));  // open: Qn, preset, en, reset
  D_Flip_Flop d_ff_2 (.clk(CLK), .D(A0), .Q(A1));  // open: Qn, preset, en, reset
  D_Flip_Flop d_ff_3 (.clk(CLK), .D(A1), .Q(A2));  // open: Qn, preset, en, reset
  D_Flip_Flop d_ff_4 (.clk(CLK), .D(A2), .Q(A3));  // open: Qn, preset, en, reset

  // Notes on the sheet:
  //   REGISTER
endmodule

module parallel_adder__with_registers (
  input  ENABLE,
  output A2,
  output A1,
  output A0,
  output CARRY,
  output S2,
  output S1,
  output S0,
  output B2,
  output B1,
  output B0
);

  wire CLEAR_2_out, CLEAR_out, CLK2_2_out, CLK2_out, clock_1_out, full_adder_using_half_adder_2_cout,
       half_adder_1_co, t_ff_1_q, t_ff_2_q, t_ff_3_q, t_ff_4_q, t_ff_5_q, t_ff_6_q;

  Clock clock_1 (.out(clock_1_out));
  Button CLEAR (.out(CLEAR_out));
  Clock #(.highDuration(2)) CLK2 (.out(CLK2_out));
  ripple_counter ripple_counter_1 (.CLK(CLK2_out), .CLEAR(CLEAR_out), .A2(A2), .A1(A1), .A0(A0));
  Clock #(.highDuration(3)) CLK2_2 (.out(CLK2_2_out));
  ripple_counter ripple_counter_2 (.CLK(CLK2_2_out), .CLEAR(CLEAR_out), .A2(B2), .A1(B1), .A0(B0));
  Button CLEAR_2 (.out(CLEAR_2_out));
  T_Flip_Flop t_ff_1 (.clk(clock_1_out), .T(A2), .Q(t_ff_1_q), .reset(CLEAR_2_out), .en(ENABLE));  // open: Qn, preset
  full_adder_using_half_adder full_adder_using_half_adder_1 (
    .A(t_ff_2_q), .B(t_ff_1_q), .Cin(full_adder_using_half_adder_2_cout), .S(S2), .Cout(CARRY));
  T_Flip_Flop t_ff_2 (.clk(clock_1_out), .T(B2), .Q(t_ff_2_q), .reset(CLEAR_2_out), .en(ENABLE));  // open: Qn, preset
  full_adder_using_half_adder full_adder_using_half_adder_2 (
    .A(t_ff_4_q), .B(t_ff_3_q), .Cin(half_adder_1_co), .S(S1), .Cout(full_adder_using_half_adder_2_cout));
  T_Flip_Flop t_ff_3 (.clk(clock_1_out), .T(A1), .Q(t_ff_3_q), .reset(CLEAR_2_out), .en(ENABLE));  // open: Qn, preset
  T_Flip_Flop t_ff_4 (.clk(clock_1_out), .T(B1), .Q(t_ff_4_q), .reset(CLEAR_2_out), .en(ENABLE));  // open: Qn, preset
  T_Flip_Flop t_ff_5 (.clk(clock_1_out), .T(A0), .Q(t_ff_5_q), .reset(CLEAR_2_out), .en(ENABLE));  // open: Qn, preset
  half_adder half_adder_1 (.A(t_ff_6_q), .B(t_ff_5_q), .S(S0), .Co(half_adder_1_co));
  T_Flip_Flop t_ff_6 (.clk(clock_1_out), .T(B0), .Q(t_ff_6_q), .en(ENABLE));  // open: Qn, preset, reset

  // Notes on the sheet:
  //   CLK1
  //   C0UNTER
  //   C0UNTER
  //   PARALLEL ADDER
endmodule

module serial_adder_with_3_registers (
  input  A3,
  input  A2,
  input  A1,
  input  A0,
  input  B3,
  input  B2,
  input  B1,
  input  B0,
  output CARRY,
  output S3,
  output S2,
  output S1,
  output S0
);

  wire CLK_out, d_ff_1_q, full_adder_using_half_adder_1_s, multiplexer_1_out, multiplexer_2_out,
       siso_shift_1_serial_out, siso_shift_2_serial_out;
  wire [1:0] n2_bit_counter_1_s0, n2_bit_counter_2_s0;

  Clock CLK (.out(CLK_out));
  Multiplexer #(.select(2), .enable("false")) multiplexer_1 (
    .in0(A0), .in1(A1), .in2(A2), .in3(A3), .out(multiplexer_1_out), .sel(n2_bit_counter_1_s0));
  _2_bit_counter u_2_bit_counter_1 (.CLK(CLK_out), .S1(n2_bit_counter_1_s0[1]), .S0(n2_bit_counter_1_s0[0]));
  Multiplexer #(.select(2), .enable("false")) multiplexer_2 (
    .in0(B0), .in1(B1), .in2(B2), .in3(B3), .out(multiplexer_2_out), .sel(n2_bit_counter_2_s0));
  _2_bit_counter u_2_bit_counter_2 (.CLK(CLK_out), .S1(n2_bit_counter_2_s0[1]), .S0(n2_bit_counter_2_s0[0]));
  SISO_shift siso_shift_1 (.CLK(CLK_out), .SERIAL_IN(multiplexer_1_out), .SERIAL_OUT(siso_shift_1_serial_out));
  SISO_shift siso_shift_2 (.CLK(CLK_out), .SERIAL_IN(multiplexer_2_out), .SERIAL_OUT(siso_shift_2_serial_out));
  full_adder_using_half_adder full_adder_using_half_adder_1 (
    .A(siso_shift_1_serial_out), .B(siso_shift_2_serial_out), .Cin(d_ff_1_q),
    .S(full_adder_using_half_adder_1_s), .Cout(CARRY));
  D_Flip_Flop d_ff_1 (.clk(CLK_out), .D(CARRY), .Q(d_ff_1_q));  // open: Qn, preset, en, reset
  SIPO_shift sipo_shift_1 (
    .CLK(CLK_out), .SERIAL_IN(full_adder_using_half_adder_1_s), .A3(S3), .A2(S2), .A1(S1), .A0(S0));

  // Notes on the sheet:
  //   2-BIT COUNTER
  //   SISO REGISTER
  //   SISO REGISTER
  //   2-BIT COUNTER
  //   STORING CARRY BIT
  //   SIPO REGISTER
endmodule

module determining_negative_number (
  input  SIGN,
  input  A3,
  input  A2,
  input  A1,
  input  A0,
  output A3_2,
  output A2_2,
  output A1_2,
  output A0_2
);

  wire half_adder_1_co, half_adder_1_s, half_adder_2_co, half_adder_2_s, half_adder_3_co, half_adder_3_s,
       half_adder_4_s, xor_using_nand_1_s, xor_using_nand_2_s, xor_using_nand_3_s, xor_using_nand_4_s;

  xor_using_nand xor_using_nand_1 (.A(A0), .B(SIGN), .S(xor_using_nand_1_s));
  xor_using_nand xor_using_nand_2 (.A(A1), .B(SIGN), .S(xor_using_nand_2_s));
  half_adder half_adder_1 (.A(xor_using_nand_1_s), .B(SIGN), .S(half_adder_1_s), .Co(half_adder_1_co));
  Multiplexer #(.enable("false")) multiplexer_1 (.in0(A0), .in1(half_adder_1_s), .out(A0_2), .sel(SIGN));
  xor_using_nand xor_using_nand_3 (.A(A2), .B(SIGN), .S(xor_using_nand_3_s));
  half_adder half_adder_2 (.A(xor_using_nand_2_s), .B(half_adder_1_co), .S(half_adder_2_s), .Co(half_adder_2_co));
  Multiplexer #(.enable("false")) multiplexer_2 (.in0(A1), .in1(half_adder_2_s), .out(A1_2), .sel(SIGN));
  half_adder half_adder_3 (.A(xor_using_nand_3_s), .B(half_adder_2_co), .S(half_adder_3_s), .Co(half_adder_3_co));
  Multiplexer #(.enable("false")) multiplexer_3 (.in0(A2), .in1(half_adder_3_s), .out(A2_2), .sel(SIGN));
  xor_using_nand xor_using_nand_4 (.A(A3), .B(SIGN), .S(xor_using_nand_4_s));
  half_adder half_adder_4 (.A(xor_using_nand_4_s), .B(half_adder_3_co), .S(half_adder_4_s));  // open: Co
  Multiplexer #(.enable("false")) multiplexer_4 (.in0(A3), .in1(half_adder_4_s), .out(A3_2), .sel(SIGN));
endmodule

module signed_integers_adder (
  input  SIGN,
  input  A3,
  input  A2,
  input  A1,
  input  A0,
  input  SIGN_2,
  input  B3,
  input  B2,
  input  B1,
  input  B0,
  output SIGN_3,
  output CARRY,
  output S3,
  output S2,
  output S1,
  output S0,
  output IGNORED
);

  wire determining_negative_number_1_a0_2, determining_negative_number_1_a1_2,
       determining_negative_number_1_a2_2, determining_negative_number_1_a3_2,
       determining_negative_number_2_a0_2, determining_negative_number_2_a1_2,
       determining_negative_number_2_a2_2, determining_negative_number_2_a3_2,
       full_adder_using_half_adder_1_cout, full_adder_using_half_adder_1_s,
       full_adder_using_half_adder_2_cout, full_adder_using_half_adder_2_s, full_adder_using_half_adder_3_s,
       half_adder_1_co, half_adder_1_s, half_adder_2_co, half_adder_2_s;

  determining_negative_number determining_negative_number_1 (
    .SIGN(SIGN), .A3(A3), .A2(A2), .A1(A1), .A0(A0), .A3_2(determining_negative_number_1_a3_2),
    .A2_2(determining_negative_number_1_a2_2), .A1_2(determining_negative_number_1_a1_2),
    .A0_2(determining_negative_number_1_a0_2));
  determining_negative_number determining_negative_number_2 (
    .SIGN(SIGN_2), .A3(B3), .A2(B2), .A1(B1), .A0(B0), .A3_2(determining_negative_number_2_a3_2),
    .A2_2(determining_negative_number_2_a2_2), .A1_2(determining_negative_number_2_a1_2),
    .A0_2(determining_negative_number_2_a0_2));
  half_adder half_adder_1 (
    .A(determining_negative_number_1_a0_2), .B(determining_negative_number_2_a0_2), .S(half_adder_1_s),
    .Co(half_adder_1_co));
  full_adder_using_half_adder full_adder_using_half_adder_1 (
    .A(determining_negative_number_1_a1_2), .B(determining_negative_number_2_a1_2), .Cin(half_adder_1_co),
    .S(full_adder_using_half_adder_1_s), .Cout(full_adder_using_half_adder_1_cout));
  full_adder_using_half_adder full_adder_using_half_adder_2 (
    .A(determining_negative_number_1_a2_2), .B(determining_negative_number_2_a2_2),
    .Cin(full_adder_using_half_adder_1_cout), .S(full_adder_using_half_adder_2_s),
    .Cout(full_adder_using_half_adder_2_cout));
  half_adder half_adder_2 (.A(SIGN), .B(SIGN_2), .S(half_adder_2_s), .Co(half_adder_2_co));
  full_adder_using_half_adder full_adder_using_half_adder_3 (
    .A(determining_negative_number_1_a3_2), .B(determining_negative_number_2_a3_2),
    .Cin(full_adder_using_half_adder_2_cout), .S(full_adder_using_half_adder_3_s), .Cout(CARRY));
  determining_negative_number determining_negative_number_3 (
    .SIGN(SIGN_3), .A3(full_adder_using_half_adder_3_s), .A2(full_adder_using_half_adder_2_s),
    .A1(full_adder_using_half_adder_1_s), .A0(half_adder_1_s), .A3_2(S3), .A2_2(S2), .A1_2(S1), .A0_2(S0));
  half_adder half_adder_3 (.A(CARRY), .B(half_adder_2_s), .S(SIGN_3), .Co(IGNORED));
  // also tied to GND on the sheet: half_adder_2_co

  // Notes on the sheet:
  //   checks sign and gives corrected input
  //   checks sign and gives corrected input
  //   OUTPUT
  //   checks sign and gives corrected output
endmodule

module serial_adder_with_2_registers (
  input  A3,
  input  A2,
  input  A1,
  input  A0,
  input  SHIFT,
  input  B3,
  input  B2,
  input  B1,
  input  B0
);

  wire CLOCK_out, d_ff_1_q, full_adder_using_half_adder_1_cout, full_adder_using_half_adder_1_s, LOAD_out,
       shift_register_1_out, shift_register_2_out;

  Button LOAD (.out(LOAD_out));
  Clock CLOCK (.out(CLOCK_out));
  Shift_Register #(.length(4)) shift_register_1 (
    .shift(SHIFT), .in(full_adder_using_half_adder_1_s), .clk(CLOCK_out), .out(shift_register_1_out),
    .load(LOAD_out), .d0(A3), .d1(A2), .d2(A1), .d3(A0));  // open: clr, q0, q1, q2, q3
  Shift_Register #(.length(4)) shift_register_2 (
    .shift(SHIFT), .in(shift_register_2_out), .clk(CLOCK_out), .out(shift_register_2_out), .load(LOAD_out),
    .d0(B3), .d1(B2), .d2(B1), .d3(B0));  // open: clr, q0, q1, q2, q3
  full_adder_using_half_adder full_adder_using_half_adder_1 (
    .A(shift_register_1_out), .B(shift_register_2_out), .Cin(d_ff_1_q), .S(full_adder_using_half_adder_1_s),
    .Cout(full_adder_using_half_adder_1_cout));
  D_Flip_Flop d_ff_1 (
    .clk(CLOCK_out), .D(full_adder_using_half_adder_1_cout), .Q(d_ff_1_q));  // open: Qn, preset, en, reset

  // Notes on the sheet:
  //   stores the sum of the full adder
  //   REGISTER 2
  //   REGISTER 1
  //   SERIAL ADDER
  //   STORING CARRY BIT
endmodule

module PIPO_register (
  input  A2,
  input  CLK,
  input  A1,
  input  A0,
  input  ENABLE,
  input  CLEAR,
  input  S2,
  input  S1,
  input  S0
);

  T_Flip_Flop t_ff_1 (.clk(CLK), .T(A0), .Q(S0), .reset(CLEAR), .en(ENABLE));  // open: Qn, preset
  T_Flip_Flop t_ff_2 (.clk(CLK), .T(A1), .Q(S1), .reset(CLEAR), .en(ENABLE));  // open: Qn, preset
  T_Flip_Flop t_ff_3 (.clk(CLK), .T(A2), .Q(S2), .reset(CLEAR), .en(ENABLE));  // open: Qn, preset

  // Notes on the sheet:
  //   PIPO REGISTER
endmodule
