// Logisim project FINAL CIRCUIT.circ as structural Verilog: 4 circuits, main circuit main
module main (
  input  A,
  input  B,
  input  C,
  input  D,
  output A_prime_B_B_prime_C_C_prime_D
);

  wire A_prime_out, B_prime_out, C_prime_out, nand_1_out, nand_2_out, nand_3_out, nand_4_out, nand_5_out,
       nand_6_out, nand_7_out, nand_8_out, nand_9_out, nand_10_out, nand_11_out;

  nand A_prime (A_prime_out, A, A);
  nand B_prime (B_prime_out, B, B);
  nand C_prime (C_prime_out, C, C);
  nand nand_1 (nand_1_out, A_prime_out, B);
  nand nand_2 (nand_2_out, B_prime_out, C);
  nand nand_3 (nand_3_out, C_prime_out, D);
  nand nand_4 (nand_4_out, nand_1_out, nand_1_out);
  nand nand_5 (nand_5_out, nand_2_out, nand_2_out);
  nand nand_6 (nand_6_out, nand_3_out, nand_3_out);
  nand nand_7 (nand_7_out, nand_4_out, nand_4_out);
  nand nand_8 (nand_8_out, nand_5_out, nand_5_out);
  nand nand_9 (nand_9_out, nand_6_out, nand_6_out);
  nand nand_10 (nand_10_out, nand_7_out, nand_8_out);
  nand nand_11 (nand_11_out, nand_10_out, nand_10_out);
  nand nand_12 (A_prime_B_B_prime_C_C_prime_D, nand_11_out, nand_9_out);

  // Notes on the sheet:
  //   A'B
  //   B'C
  //   C'D
  //   A'B+B'C
endmodule

module odd_parity_generator (
  input  A2,
  input  A1,
  input  A0,
  output ODD_PARITY_BIT
);

  wire xor_using_nand_1_s, xor_using_nand_2_s;

  xor_using_nand xor_using_nand_1 (.A(A0), .B(A1), .S(xor_using_nand_1_s));
  xor_using_nand xor_using_nand_2 (.A(xor_using_nand_1_s), .B(A2), .S(xor_using_nand_2_s));
  not_using_nand not_using_nand_1 (.in_1(xor_using_nand_2_s), .out_2(ODD_PARITY_BIT));

  // Notes on the sheet:
  //   3-BIT INPUT
  //   ODD PARITY GENERATOR
endmodule

// XOR
module xor_using_nand (
  input  A,
  input  B,
  output S
);

  wire nand_1_out, nand_2_out, nand_3_out;

  nand nand_1 (nand_1_out, A, B);
  nand nand_2 (nand_2_out, A, nand_1_out);
  nand nand_3 (nand_3_out, nand_1_out, B);
  nand nand_4 (S, nand_2_out, nand_3_out);
endmodule

// NOT
module not_using_nand (
  input  in_1,
  output out_2
);

  nand nand_1 (out_2, in_1, in_1);
endmodule
