// Logisim project lab_exp.circ as structural Verilog: 2 circuits, main circuit main
module main (
  input  G3,
  input  G2,
  input  G1,
  input  G0,
  output B3,
  output B2,
  output B1,
  output B0
);

  xor_using_nand xor_using_nand_1 (.A(G3), .B(G2), .A_XOR_B(B2));
  xor_using_nand xor_using_nand_2 (.A(B2), .B(G1), .A_XOR_B(B1));
  xor_using_nand xor_using_nand_3 (.A(B1), .B(G0), .A_XOR_B(B0));

  assign B3 = G3;

  // Notes on the sheet:
  //   4-BIT GRAY CODE INPUT
  //   GRAY CODE TO BINARY CONVERTOR USING NAND GATES ONLY
  //   4-BIT BINARY OUTPUT
endmodule

// XOR
module xor_using_nand (
  input  A,
  input  B,
  output A_XOR_B
);

  wire nand_1_out, nand_2_out, nand_3_out;

  nand nand_1 (nand_1_out, A, B);
  nand nand_2 (nand_2_out, A, nand_1_out);
  nand nand_3 (nand_3_out, nand_1_out, B);
  nand nand_4 (A_XOR_B, nand_2_out, nand_3_out);

  // Notes on the sheet:
  //   XOR USING NAND GATES
endmodule
