// Logisim project clock.circ as structural Verilog: 6 circuits, main circuit main
module main (
  input  I1,
  input  I0,
  input  I3,
  input  I2,
  input  I1_2,
  input  I0_2,
  input  I2_2,
  input  I1_3,
  input  I0_3,
  input  I3_2,
  input  I2_3,
  input  I1_4,
  input  I0_4,
  input  I2_4,
  input  I1_5,
  input  I0_5,
  input  I3_3,
  input  I2_5,
  input  I1_6,
  input  I0_6,
  input  UP_COUNT,
  input  PARALLEL_LOAD
);

  wire and_1_out, and_2_out, and_3_out, and_4_out, CLEAR_out, CLOCK_out, multiplexer_1_out, multiplexer_2_out;
  wire [1:0] mod_24_1_p0;
  wire [2:0] mod_60_1_p0, mod_60_2_p0;
  wire [3:0] mod_24_1_q0, mod_60_1_q0, mod_60_2_q0;

  mod_24 mod_24_1 (
    .CLOCK(multiplexer_1_out), .CLEAR(CLEAR_out), .I3(I3), .I2(I2), .I1(I1_2), .I0(I0_2), .COUNT(UP_COUNT),
    .LOAD(PARALLEL_LOAD), .I1_2(I1), .I0_2(I0), .q0(mod_24_1_q0[0]), .q1(mod_24_1_q0[1]),
    .q2(mod_24_1_q0[2]), .q3(mod_24_1_q0[3]), .p0(mod_24_1_p0[0]), .p1(mod_24_1_p0[1]));
  Hex_Digit_Display hex_digit_display_1 (.value(mod_24_1_q0));  // open: dp
  Hex_Digit_Display hex_digit_display_2 (.value({2'b00, mod_24_1_p0}));  // open: dp
  and and_1 (and_1_out, multiplexer_2_out, mod_60_1_p0[0], mod_60_1_p0[2], 1'b1, and_2_out);
  Multiplexer #(.enable("false")) multiplexer_1 (
    .in0(and_1_out), .in1(CLOCK_out), .out(multiplexer_1_out), .sel(PARALLEL_LOAD));
  Button CLEAR (.out(CLEAR_out));
  mod_60 mod_60_1 (
    .CLOCK(multiplexer_2_out), .CLEAR(CLEAR_out), .I3(I3_2), .I2(I2_3), .I1(I1_4), .I0(I0_4),
    .COUNT(UP_COUNT), .LOAD(PARALLEL_LOAD), .I2_2(I2_2), .I1_2(I1_3), .I0_2(I0_3), .q3(mod_60_1_q0[3]),
    .q2(mod_60_1_q0[2]), .q1(mod_60_1_q0[1]), .q0(mod_60_1_q0[0]), .p2(mod_60_1_p0[2]), .p1(mod_60_1_p0[1]),
    .p0(mod_60_1_p0[0]));
  Hex_Digit_Display hex_digit_display_3 (.value(mod_60_1_q0));  // open: dp
  Hex_Digit_Display hex_digit_display_4 (.value({1'b0, mod_60_1_p0}));  // open: dp
  and and_2 (and_2_out, mod_60_1_q0[3], mod_60_1_q0[0]);
  Multiplexer #(.enable("false")) multiplexer_2 (
    .in0(and_3_out), .in1(CLOCK_out), .out(multiplexer_2_out), .sel(PARALLEL_LOAD));
  and and_3 (and_3_out, mod_60_2_p0[0], mod_60_2_p0[2], CLOCK_out, and_4_out, 1'b1);
  Clock CLOCK (.out(CLOCK_out));
  Hex_Digit_Display hex_digit_display_5 (.value(mod_60_2_q0));  // open: dp
  Hex_Digit_Display hex_digit_display_6 (.value({1'b0, mod_60_2_p0}));  // open: dp
  mod_60 mod_60_2 (
    .CLOCK(CLOCK_out), .CLEAR(CLEAR_out), .I3(I3_3), .I2(I2_5), .I1(I1_6), .I0(I0_6), .COUNT(UP_COUNT),
    .LOAD(PARALLEL_LOAD), .I2_2(I2_4), .I1_2(I1_5), .I0_2(I0_5), .q3(mod_60_2_q0[3]), .q2(mod_60_2_q0[2]),
    .q1(mod_60_2_q0[1]), .q0(mod_60_2_q0[0]), .p2(mod_60_2_p0[2]), .p1(mod_60_2_p0[1]), .p0(mod_60_2_p0[0]));
  and and_4 (and_4_out, mod_60_2_q0[3], mod_60_2_q0[0]);

  // Notes on the sheet:
  //   HH
  //   CLOCK
  //   MM
  //   (with parallel loading)
  //   SS
endmodule

module decade (
  input  COUNT,
  input  LOAD,
  input  i0,
  input  i1,
  input  i2,
  input  i3,
  input  CLEAR,
  input  CLOCK,
  output q0,
  output q1,
  output q2,
  output q3
);

  wire and_1_out, and_2_out, and_3_out, and_4_out, and_5_out, and_6_out, and_7_out, and_8_out, and_9_out,
       and_10_out, and_11_out, and_12_out, and_13_out, not_1_out, not_2_out, not_3_out, not_4_out, not_5_out,
       or_1_out, or_2_out, or_3_out, or_4_out, or_5_out, or_6_out, or_7_out, or_8_out, or_9_out;

  not not_1 (not_1_out, i0);
  not not_2 (not_2_out, i1);
  not not_3 (not_3_out, i2);
  not not_4 (not_4_out, i3);
  and and_1 (and_1_out, COUNT, not_5_out);
  not not_5 (not_5_out, LOAD);
  and and_2 (and_2_out, i0, LOAD);
  and and_3 (and_3_out, not_1_out, LOAD);
  and and_4 (and_4_out, i1, LOAD);
  and and_5 (and_5_out, LOAD, not_2_out);
  and and_6 (and_6_out, i2, LOAD);
  and and_7 (and_7_out, not_3_out, LOAD);
  and and_8 (and_8_out, i3, LOAD);
  and and_9 (and_9_out, not_4_out, LOAD);
  and and_10 (and_10_out, q1, q3);
  and and_11 (and_11_out, q0, and_1_out);
  and and_12 (and_12_out, and_1_out, q0, q1);
  and and_13 (and_13_out, q2, q1, q0, and_1_out);
  or or_1 (or_1_out, and_10_out, CLEAR);
  or or_2 (or_2_out, and_2_out, and_1_out);
  or or_3 (or_3_out, and_3_out, and_1_out);
  or or_4 (or_4_out, and_4_out, and_11_out);
  or or_5 (or_5_out, and_11_out, and_5_out);
  or or_6 (or_6_out, and_6_out, and_12_out);
  or or_7 (or_7_out, and_12_out, and_7_out);
  or or_8 (or_8_out, and_8_out, and_13_out);
  or or_9 (or_9_out, and_13_out, and_9_out);
  J_K_Flip_Flop #(.trigger("falling")) j_k_ff_1 (
    .J(or_2_out), .clk(CLOCK), .K(or_3_out), .Q(q0), .reset(or_1_out));  // open: Qn, preset, en
  J_K_Flip_Flop #(.trigger("falling")) j_k_ff_2 (
    .J(or_4_out), .clk(CLOCK), .K(or_5_out), .Q(q1), .reset(or_1_out));  // open: Qn, preset, en
  J_K_Flip_Flop #(.trigger("falling")) j_k_ff_3 (
    .J(or_6_out), .clk(CLOCK), .K(or_7_out), .Q(q2), .reset(or_1_out));  // open: Qn, preset, en
  J_K_Flip_Flop #(.trigger("falling")) j_k_ff_4 (
    .J(or_8_out), .clk(CLOCK), .K(or_9_out), .Q(q3), .reset(or_1_out));  // open: Qn, preset, en

  // Notes on the sheet:
  //   DECADE COUNTER
  //   (with parallel loading)
endmodule

module mod_6 (
  input  COUNT,
  input  LOAD,
  input  i0,
  input  i1,
  input  i2,
  input  i3,
  input  CLEAR,
  input  CLOCK,
  output q0,
  output q1,
  output q2,
  output q3
);

  wire and_1_out, and_2_out, and_3_out, and_4_out, and_5_out, and_6_out, and_7_out, and_8_out, and_9_out,
       and_10_out, and_11_out, and_12_out, and_13_out, not_1_out, not_2_out, not_3_out, not_4_out, not_5_out,
       or_1_out, or_2_out, or_3_out, or_4_out, or_5_out, or_6_out, or_7_out, or_8_out, or_9_out;

  not not_1 (not_1_out, i0);
  not not_2 (not_2_out, i1);
  not not_3 (not_3_out, i2);
  not not_4 (not_4_out, i3);
  and and_1 (and_1_out, COUNT, not_5_out);
  not not_5 (not_5_out, LOAD);
  and and_2 (and_2_out, i0, LOAD);
  and and_3 (and_3_out, not_1_out, LOAD);
  and and_4 (and_4_out, i1, LOAD);
  and and_5 (and_5_out, LOAD, not_2_out);
  and and_6 (and_6_out, i2, LOAD);
  and and_7 (and_7_out, not_3_out, LOAD);
  and and_8 (and_8_out, i3, LOAD);
  and and_9 (and_9_out, not_4_out, LOAD);
  and and_10 (and_10_out, q1, q2);
  and and_11 (and_11_out, q0, and_1_out);
  and and_12 (and_12_out, and_1_out, q0, q1);
  and and_13 (and_13_out, q2, q1, q0, and_1_out);
  or or_1 (or_1_out, and_10_out, CLEAR);
  or or_2 (or_2_out, and_2_out, and_1_out);
  or or_3 (or_3_out, and_3_out, and_1_out);
  or or_4 (or_4_out, and_4_out, and_11_out);
  or or_5 (or_5_out, and_11_out, and_5_out);
  or or_6 (or_6_out, and_6_out, and_12_out);
  or or_7 (or_7_out, and_12_out, and_7_out);
  or or_8 (or_8_out, and_8_out, and_13_out);
  or or_9 (or_9_out, and_13_out, and_9_out);
  J_K_Flip_Flop #(.trigger("falling")) j_k_ff_1 (
    .J(or_2_out), .clk(CLOCK), .K(or_3_out), .Q(q0), .reset(or_1_out));  // open: Qn, preset, en
  J_K_Flip_Flop #(.trigger("falling")) j_k_ff_2 (
    .J(or_4_out), .clk(CLOCK), .K(or_5_out), .Q(q1), .reset(or_1_out));  // open: Qn, preset, en
  J_K_Flip_Flop #(.trigger("falling")) j_k_ff_3 (
    .J(or_6_out), .clk(CLOCK), .K(or_7_out), .Q(q2), .reset(or_1_out));  // open: Qn, preset, en
  J_K_Flip_Flop #(.trigger("falling")) j_k_ff_4 (
    .J(or_8_out), .clk(CLOCK), .K(or_9_out), .Q(q3), .reset(or_1_out));  // open: Qn, preset, en

  // Notes on the sheet:
  //   MOD 6 COUNTER
  //   (with parallel loading)
endmodule

module mod_3 (
  input  COUNT,
  input  LOAD,
  input  i0,
  input  i1,
  input  i2,
  input  i3,
  input  CLEAR,
  input  CLOCK,
  output q0,
  output q1,
  output q2,
  output q3
);

  wire and_1_out, and_2_out, and_3_out, and_4_out, and_5_out, and_6_out, and_7_out, and_8_out, and_9_out,
       and_10_out, and_11_out, and_12_out, and_13_out, not_1_out, not_2_out, not_3_out, not_4_out, not_5_out,
       or_1_out, or_2_out, or_3_out, or_4_out, or_5_out, or_6_out, or_7_out, or_8_out, or_9_out;

  not not_1 (not_1_out, i0);
  not not_2 (not_2_out, i1);
  not not_3 (not_3_out, i2);
  not not_4 (not_4_out, i3);
  and and_1 (and_1_out, COUNT, not_5_out);
  not not_5 (not_5_out, LOAD);
  and and_2 (and_2_out, i0, LOAD);
  and and_3 (and_3_out, not_1_out, LOAD);
  and and_4 (and_4_out, i1, LOAD);
  and and_5 (and_5_out, LOAD, not_2_out);
  and and_6 (and_6_out, i2, LOAD);
  and and_7 (and_7_out, not_3_out, LOAD);
  and and_8 (and_8_out, i3, LOAD);
  and and_9 (and_9_out, not_4_out, LOAD);
  and and_10 (and_10_out, q1, q0);
  and and_11 (and_11_out, q0, and_1_out);
  and and_12 (and_12_out, and_1_out, q0, q1);
  and and_13 (and_13_out, q2, q1, q0, and_1_out);
  or or_1 (or_1_out, and_10_out, CLEAR);
  or or_2 (or_2_out, and_2_out, and_1_out);
  or or_3 (or_3_out, and_3_out, and_1_out);
  or or_4 (or_4_out, and_4_out, and_11_out);
  or or_5 (or_5_out, and_11_out, and_5_out);
  or or_6 (or_6_out, and_6_out, and_12_out);
  or or_7 (or_7_out, and_12_out, and_7_out);
  or or_8 (or_8_out, and_8_out, and_13_out);
  or or_9 (or_9_out, and_13_out, and_9_out);
  J_K_Flip_Flop #(.trigger("falling")) j_k_ff_1 (
    .J(or_2_out), .clk(CLOCK), .K(or_3_out), .Q(q0), .reset(or_1_out));  // open: Qn, preset, en
  J_K_Flip_Flop #(.trigger("falling")) j_k_ff_2 (
    .J(or_4_out), .clk(CLOCK), .K(or_5_out), .Q(q1), .reset(or_1_out));  // open: Qn, preset, en
  J_K_Flip_Flop #(.trigger("falling")) j_k_ff_3 (
    .J(or_6_out), .clk(CLOCK), .K(or_7_out), .Q(q2), .reset(or_1_out));  // open: Qn, preset, en
  J_K_Flip_Flop #(.trigger("falling")) j_k_ff_4 (
    .J(or_8_out), .clk(CLOCK), .K(or_9_out), .Q(q3), .reset(or_1_out));  // open: Qn, preset, en

  // Notes on the sheet:
  //   MOD 3 COUNTER
  //   (with parallel loading)
endmodule

module mod_60 (
  input  I3,
  input  I2,
  input  I1,
  input  I0,
  input  COUNT,
  input  LOAD,
  input  CLOCK,
  input  CLEAR,
  input  I2_2,
  input  I1_2,
  input  I0_2,
  output q3,
  output q2,
  output q1,
  output q0,
  output p2,
  output p1,
  output p0
);

  wire and_1_out, multiplexer_1_out;

  decade decade_1 (
    .COUNT(COUNT), .LOAD(LOAD), .i0(I0), .i1(I1), .i2(I2), .i3(I3), .CLEAR(CLEAR), .CLOCK(CLOCK), .q0(q0),
    .q1(q1), .q2(q2), .q3(q3));
  and and_1 (and_1_out, COUNT, CLOCK, q3, q0);
  Multiplexer #(.enable("false")) multiplexer_1 (.in0(and_1_out), .in1(CLOCK), .out(multiplexer_1_out), .sel(LOAD));
  mod_6 mod_6_1 (
    .COUNT(COUNT), .LOAD(LOAD), .i0(I0_2), .i1(I1_2), .i2(I2_2), .i3(1'b0), .CLEAR(CLEAR),
    .CLOCK(multiplexer_1_out), .q0(p0), .q1(p1), .q2(p2));  // open: q3

  // Notes on the sheet:
  //   MOD 60 COUNTER
  //   (with parallel loading)
endmodule

module mod_24 (
  input  I3,
  input  I2,
  input  I1,
  input  I0,
  input  COUNT,
  input  LOAD,
  input  CLOCK,
  input  CLEAR,
  input  I1_2,
  input  I0_2,
  output q0,
  output q1,
  output q2,
  output q3,
  output p0,
  output p1
);

  wire and_1_out, and_2_out, mod_3_1_q2, mod_3_1_q3, multiplexer_1_out, or_1_out;

  or or_1 (or_1_out, and_2_out, CLEAR);
  decade decade_1 (
    .COUNT(COUNT), .LOAD(LOAD), .i0(I0), .i1(I1), .i2(I2), .i3(I3), .CLEAR(or_1_out), .CLOCK(CLOCK), .q0(q0),
    .q1(q1), .q2(q2), .q3(q3));
  mod_3 mod_3_1 (
    .COUNT(COUNT), .LOAD(LOAD), .i0(I0_2), .i1(I1_2), .i2(1'b0), .i3(1'b0), .CLEAR(or_1_out),
    .CLOCK(multiplexer_1_out), .q0(p0), .q1(p1), .q2(mod_3_1_q2), .q3(mod_3_1_q3));
  and and_1 (and_1_out, COUNT, CLOCK, q3, q0);
  Multiplexer #(.enable("false")) multiplexer_1 (.in0(and_1_out), .in1(CLOCK), .out(multiplexer_1_out), .sel(LOAD));
  and and_2 (and_2_out, q2, p1);
  // also tied to GND on the sheet: {mod_3_1_q2, mod_3_1_q3}

  // Notes on the sheet:
  //   MOD 24 COUNTER
  //   (with parallel loading)
endmodule
