// Logisim project hardware_lab.circ as structural Verilog: 19 circuits, main circuit main
module main2 (
  input  CONTROL,
  input  CLOCK,
  input  CLEAR,
  output Q3,
  output Q2,
  output Q1,
  output Q0
);

  wire and_using_nand_1_s, and_using_nand_2_s, and_using_nand_3_s, j_k_ff_1_qn, j_k_ff_2_qn, j_k_ff_3_qn,
       j_k_ff_4_qn, mini_circ_1_out_4, n3_input_and_using_nand_1_s, n3_input_and_using_nand_2_s,
       n3_input_and_using_nand_3_s, n3_input_and_using_nand_4_s, n3_input_and_using_nand_5_s,
       n3_input_and_using_nand_6_s, not_using_nand_1_a_prime, or_using_nand_1_s, or_using_nand_2_s,
       or_using_nand_3_s, or_using_nand_4_s, xor_using_nand_1_s;

  not_using_nand not_using_nand_1 (.A(CONTROL), .A_prime(not_using_nand_1_a_prime));
  J_K_Flip_Flop #(.trigger("falling")) j_k_ff_1 (
    .J(1'b1), .clk(CLOCK), .K(1'b1), .Q(Q0), .Qn(j_k_ff_1_qn), .reset(CLEAR));  // open: preset, en
  _3_input_and_using_nand u_3_input_and_using_nand_1 (
    .A(Q0), .B(j_k_ff_4_qn), .C(not_using_nand_1_a_prime), .S(n3_input_and_using_nand_1_s));
  or_using_nand or_using_nand_1 (.A(and_using_nand_1_s), .B(n3_input_and_using_nand_1_s), .S(or_using_nand_1_s));
  mini_circ mini_circ_1 (.Q2(Q2), .Q3(Q3), .Q0_prime(j_k_ff_1_qn), .out_4(mini_circ_1_out_4));
  and_using_nand and_using_nand_1 (.A(mini_circ_1_out_4), .B(CONTROL), .S(and_using_nand_1_s));
  J_K_Flip_Flop #(.trigger("falling")) j_k_ff_2 (
    .J(or_using_nand_1_s), .clk(CLOCK), .K(xor_using_nand_1_s), .Q(Q1), .Qn(j_k_ff_2_qn), .reset(CLEAR));  // open: preset, en
  _3_input_and_using_nand u_3_input_and_using_nand_2 (
    .A(Q0), .B(Q1), .C(not_using_nand_1_a_prime), .S(n3_input_and_using_nand_2_s));
  _3_input_and_using_nand u_3_input_and_using_nand_3 (
    .A(CONTROL), .B(Q3), .C(j_k_ff_1_qn), .S(n3_input_and_using_nand_3_s));
  or_using_nand or_using_nand_2 (
    .A(n3_input_and_using_nand_2_s), .B(n3_input_and_using_nand_3_s), .S(or_using_nand_2_s));
  or_using_nand or_using_nand_3 (
    .A(n3_input_and_using_nand_4_s), .B(n3_input_and_using_nand_2_s), .S(or_using_nand_3_s));
  _3_input_and_using_nand u_3_input_and_using_nand_4 (
    .A(j_k_ff_1_qn), .B(CONTROL), .C(j_k_ff_2_qn), .S(n3_input_and_using_nand_4_s));
  J_K_Flip_Flop #(.trigger("falling")) j_k_ff_3 (
    .J(or_using_nand_2_s), .clk(CLOCK), .K(or_using_nand_3_s), .Q(Q2), .Qn(j_k_ff_3_qn), .reset(CLEAR));  // open: preset, en
  and_using_nand and_using_nand_2 (
    .A(n3_input_and_using_nand_5_s), .B(not_using_nand_1_a_prime), .S(and_using_nand_2_s));
  or_using_nand or_using_nand_4 (.A(and_using_nand_3_s), .B(and_using_nand_2_s), .S(or_using_nand_4_s));
  J_K_Flip_Flop #(.trigger("falling")) j_k_ff_4 (
    .J(or_using_nand_4_s), .clk(CLOCK), .K(xor_using_nand_1_s), .Q(Q3), .Qn(j_k_ff_4_qn), .reset(CLEAR));  // open: preset, en
  xor_using_nand xor_using_nand_1 (.A(Q0), .B(CONTROL), .S(xor_using_nand_1_s));
  _3_input_and_using_nand u_3_input_and_using_nand_5 (.A(Q0), .B(Q1), .C(Q2), .S(n3_input_and_using_nand_5_s));
  and_using_nand and_using_nand_3 (.A(CONTROL), .B(n3_input_and_using_nand_6_s), .S(and_using_nand_3_s));
  _3_input_and_using_nand u_3_input_and_using_nand_6 (
    .A(j_k_ff_1_qn), .B(j_k_ff_2_qn), .C(j_k_ff_3_qn), .S(n3_input_and_using_nand_6_s));

  // Notes on the sheet:
  //   UP (0) / DOWN (1)
  //   FF0
  //   Q0'(Q2 + Q3)
  //   FF1
  //   FF2
  //   DECADE COUNTER
  //   (without parallel loading)
  //   FF3
  //   OUTPUT
endmodule

module cascaded_decade (
  input  CONTROL
);

  wire and_1_out, and_using_nand_1_s, and_using_nand_2_s, button_1_out, CLOCK_out,
       n3_input_and_using_nand_1_s, not_1_out, not_2_out, not_3_out, not_4_out, not_5_out, or_using_nand_1_s;
  wire [3:0] main2_1_q0, main2_2_q0;

  Button button_1 (.out(button_1_out));
  Clock CLOCK (.out(CLOCK_out));
  main2 main2_1 (
    .CLOCK(CLOCK_out), .CLEAR(button_1_out), .CONTROL(CONTROL), .Q3(main2_1_q0[3]), .Q2(main2_1_q0[2]),
    .Q1(main2_1_q0[1]), .Q0(main2_1_q0[0]));
  not not_1 (not_1_out, CONTROL);
  _3_input_and_using_nand u_3_input_and_using_nand_1 (
    .A(not_1_out), .B(main2_1_q0[0]), .C(main2_1_q0[3]), .S(n3_input_and_using_nand_1_s));
  or_using_nand or_using_nand_1 (.A(and_using_nand_2_s), .B(n3_input_and_using_nand_1_s), .S(or_using_nand_1_s));
  and_using_nand and_using_nand_1 (.A(or_using_nand_1_s), .B(CLOCK_out), .S(and_using_nand_1_s));
  main2 main2_2 (
    .CLOCK(and_using_nand_1_s), .CLEAR(button_1_out), .CONTROL(CONTROL), .Q3(main2_2_q0[3]),
    .Q2(main2_2_q0[2]), .Q1(main2_2_q0[1]), .Q0(main2_2_q0[0]));
  and_using_nand and_using_nand_2 (.A(CONTROL), .B(and_1_out), .S(and_using_nand_2_s));
  not not_2 (not_2_out, main2_1_q0[1]);
  not not_3 (not_3_out, main2_1_q0[3]);
  not not_4 (not_4_out, main2_1_q0[2]);
  not not_5 (not_5_out, main2_1_q0[0]);
  and and_1 (and_1_out, not_3_out, not_4_out, not_2_out, not_5_out);
  Hex_Digit_Display hex_digit_display_1 (.value(main2_2_q0));  // open: dp
  Hex_Digit_Display hex_digit_display_2 (.value(main2_1_q0));  // open: dp

  // Notes on the sheet:
  //   CLEAR
  //   decade counter 2
  //   decade counter 1
  //   UP (0) / DOWN (1)
  //   7-segment display
  //   CASCADED DECADE
endmodule

module _7_seg_decade (
  input  CONTROL
);

  wire CLOCK_out, main2_1_q0, main2_1_q1, main2_1_q2, main2_1_q3, n7segment_decoder_1_a_2,
       n7segment_decoder_1_b_2, n7segment_decoder_1_c_2, n7segment_decoder_1_d_2, n7segment_decoder_1_e,
       n7segment_decoder_1_f, n7segment_decoder_1_g;

  Clock CLOCK (.out(CLOCK_out));
  main2 main2_1 (
    .CLOCK(CLOCK_out), .CONTROL(CONTROL), .Q3(main2_1_q3), .Q2(main2_1_q2), .Q1(main2_1_q1), .Q0(main2_1_q0));  // open: CLEAR
  _7segment_decoder u_7segment_decoder_1 (
    .D(main2_1_q3), .C(main2_1_q2), .B(main2_1_q1), .A(main2_1_q0), .a_2(n7segment_decoder_1_a_2),
    .b_2(n7segment_decoder_1_b_2), .c_2(n7segment_decoder_1_c_2), .d_2(n7segment_decoder_1_d_2),
    .e(n7segment_decoder_1_e), .f(n7segment_decoder_1_f), .g(n7segment_decoder_1_g));
  _7_Segment_Display u_7_segment_display_1 (
    .g(n7segment_decoder_1_g), .f(n7segment_decoder_1_f), .a(n7segment_decoder_1_a_2),
    .b(n7segment_decoder_1_b_2), .e(n7segment_decoder_1_e), .d(n7segment_decoder_1_d_2),
    .c(n7segment_decoder_1_c_2));  // open: dp

  // Notes on the sheet:
  //   decade counter
  //   UP (0) / DOWN (1)
  //   bcd to 7 seg decoder
endmodule

module _0_59_counter (
  input  CONTROL
);

  wire and_1_out, and_using_nand_1_s, and_using_nand_2_s, button_1_out, clock_1_out, main2_1_q0, main2_1_q1,
       main2_1_q2, main2_1_q3, mod_6_counter_1_q0, mod_6_counter_1_q1, mod_6_counter_1_q2,
       n3_input_and_using_nand_1_s, n7segment_decoder_1_a_2, n7segment_decoder_1_b_2,
       n7segment_decoder_1_c_2, n7segment_decoder_1_d_2, n7segment_decoder_1_e, n7segment_decoder_1_f,
       n7segment_decoder_1_g, n7segment_decoder_2_a_2, n7segment_decoder_2_b_2, n7segment_decoder_2_c_2,
       n7segment_decoder_2_d_2, n7segment_decoder_2_e, n7segment_decoder_2_f, n7segment_decoder_2_g,
       not_1_out, not_2_out, not_3_out, not_4_out, not_using_nand_1_a_prime, or_using_nand_1_s;

  Button button_1 (.out(button_1_out));
  Clock clock_1 (.out(clock_1_out));
  main2 main2_1 (
    .CLOCK(clock_1_out), .CLEAR(button_1_out), .CONTROL(CONTROL), .Q3(main2_1_q3), .Q2(main2_1_q2),
    .Q1(main2_1_q1), .Q0(main2_1_q0));
  not_using_nand not_using_nand_1 (.A(CONTROL), .A_prime(not_using_nand_1_a_prime));
  _3_input_and_using_nand u_3_input_and_using_nand_1 (
    .A(not_using_nand_1_a_prime), .B(main2_1_q3), .C(main2_1_q0), .S(n3_input_and_using_nand_1_s));
  or_using_nand or_using_nand_1 (.A(and_using_nand_2_s), .B(n3_input_and_using_nand_1_s), .S(or_using_nand_1_s));
  and_using_nand and_using_nand_1 (.A(or_using_nand_1_s), .B(clock_1_out), .S(and_using_nand_1_s));
  mod_6_counter mod_6_counter_1 (
    .CONTROL(CONTROL), .CLOCK(and_using_nand_1_s), .CLEAR(button_1_out), .Q2(mod_6_counter_1_q2),
    .Q1(mod_6_counter_1_q1), .Q0(mod_6_counter_1_q0));
  not not_1 (not_1_out, main2_1_q0);
  not not_2 (not_2_out, main2_1_q1);
  not not_3 (not_3_out, main2_1_q3);
  not not_4 (not_4_out, main2_1_q2);
  and and_1 (and_1_out, not_1_out, not_3_out, not_2_out, not_4_out);
  and_using_nand and_using_nand_2 (.A(and_1_out), .B(CONTROL), .S(and_using_nand_2_s));
  _7segment_decoder u_7segment_decoder_1 (
    .D(main2_1_q3), .C(main2_1_q2), .B(main2_1_q1), .A(main2_1_q0), .a_2(n7segment_decoder_1_a_2),
    .b_2(n7segment_decoder_1_b_2), .c_2(n7segment_decoder_1_c_2), .d_2(n7segment_decoder_1_d_2),
    .e(n7segment_decoder_1_e), .f(n7segment_decoder_1_f), .g(n7segment_decoder_1_g));
  _7_Segment_Display u_7_segment_display_1 (
    .g(n7segment_decoder_2_g), .f(n7segment_decoder_2_f), .a(n7segment_decoder_2_a_2),
    .b(n7segment_decoder_2_b_2), .e(n7segment_decoder_2_e), .d(n7segment_decoder_2_d_2),
    .c(n7segment_decoder_2_c_2));  // open: dp
  _7segment_decoder u_7segment_decoder_2 (
    .D(1'b0), .C(mod_6_counter_1_q2), .B(mod_6_counter_1_q1), .A(mod_6_counter_1_q0),
    .a_2(n7segment_decoder_2_a_2), .b_2(n7segment_decoder_2_b_2), .c_2(n7segment_decoder_2_c_2),
    .d_2(n7segment_decoder_2_d_2), .e(n7segment_decoder_2_e), .f(n7segment_decoder_2_f),
    .g(n7segment_decoder_2_g));
  _7_Segment_Display u_7_segment_display_2 (
    .g(n7segment_decoder_1_g), .f(n7segment_decoder_1_f), .a(n7segment_decoder_1_a_2),
    .b(n7segment_decoder_1_b_2), .e(n7segment_decoder_1_e), .d(n7segment_decoder_1_d_2),
    .c(n7segment_decoder_1_c_2));  // open: dp

  // Notes on the sheet:
  //   CLEAR
  //   UP (0) / DOWN (1)
  //   0-59 COUNTER
  //   (without parallel loading)
endmodule

module clock (
  input  CLEAR
);

  wire and_1_out, and_using_nand_1_s, and_using_nand_2_s, CLOCK_out, main_1_out_6;
  wire [1:0] cascaded_mod_3_and_decade_1_p0;
  wire [2:0] n0_59_temp_1_p0, n0_59_temp_2_p0;
  wire [3:0] cascaded_mod_3_and_decade_1_q0, n0_59_temp_1_q0, n0_59_temp_2_q0;

  Hex_Digit_Display hex_digit_display_1 (.value(cascaded_mod_3_and_decade_1_q0));  // open: dp
  Hex_Digit_Display hex_digit_display_2 (.value({2'b00, cascaded_mod_3_and_decade_1_p0}));  // open: dp
  cascaded_mod_3_and_decade cascaded_mod_3_and_decade_1 (
    .clock(and_1_out), .clear(CLEAR), .q0(cascaded_mod_3_and_decade_1_q0[0]),
    .q1(cascaded_mod_3_and_decade_1_q0[1]), .q2(cascaded_mod_3_and_decade_1_q0[2]),
    .q3(cascaded_mod_3_and_decade_1_q0[3]), .p0(cascaded_mod_3_and_decade_1_p0[0]),
    .p1(cascaded_mod_3_and_decade_1_p0[1]));
  and and_1 (and_1_out, main_1_out_6, n0_59_temp_1_p0[0], n0_59_temp_1_p0[2], and_using_nand_1_s, 1'b1);
  Hex_Digit_Display hex_digit_display_3 (.value({1'b0, n0_59_temp_1_p0}));  // open: dp
  _0_59__temp u_0_59_temp_1 (
    .CLOCK(main_1_out_6), .CLEAR(CLEAR), .CONTROL(1'b0), .q3(n0_59_temp_1_q0[3]), .q2(n0_59_temp_1_q0[2]),
    .q1(n0_59_temp_1_q0[1]), .q0(n0_59_temp_1_q0[0]), .p2(n0_59_temp_1_p0[2]), .p1(n0_59_temp_1_p0[1]),
    .p0(n0_59_temp_1_p0[0]));
  Hex_Digit_Display hex_digit_display_4 (.value(n0_59_temp_1_q0));  // open: dp
  main main_1 (
    .control(1'b1), .units(and_using_nand_2_s), .i3(n0_59_temp_2_p0[2]), .i0(n0_59_temp_2_p0[0]),
    .clock(CLOCK_out), .out_6(main_1_out_6));
  and_using_nand and_using_nand_1 (.A(n0_59_temp_1_q0[0]), .B(n0_59_temp_1_q0[3]), .S(and_using_nand_1_s));
  Clock CLOCK (.out(CLOCK_out));
  _0_59__temp u_0_59_temp_2 (
    .CLOCK(CLOCK_out), .CLEAR(CLEAR), .CONTROL(1'b0), .q3(n0_59_temp_2_q0[3]), .q2(n0_59_temp_2_q0[2]),
    .q1(n0_59_temp_2_q0[1]), .q0(n0_59_temp_2_q0[0]), .p2(n0_59_temp_2_p0[2]), .p1(n0_59_temp_2_p0[1]),
    .p0(n0_59_temp_2_p0[0]));
  Hex_Digit_Display hex_digit_display_5 (.value({1'b0, n0_59_temp_2_p0}));  // open: dp
  Hex_Digit_Display hex_digit_display_6 (.value(n0_59_temp_2_q0));  // open: dp
  and_using_nand and_using_nand_2 (.A(n0_59_temp_2_q0[3]), .B(n0_59_temp_2_q0[0]), .S(and_using_nand_2_s));

  // Notes on the sheet:
  //   HH
  //   MM
  //   SS
endmodule

module cascaded_mod_3_and_decade (
  input  clock,
  input  clear,
  output q0,
  output q1,
  output q2,
  output q3,
  output p0,
  output p1
);

  wire and_1_out, and_using_nand_1_s, and_using_nand_2_s, n3_input_and_using_nand_1_s, not_1_out, or_1_out;

  and and_1 (and_1_out, q2, and_using_nand_1_s);
  or or_1 (or_1_out, clear, and_1_out);
  mod_3 mod_3_1 (.clock(and_using_nand_2_s), .clear(or_1_out), .q1(p1), .q0(p0));
  main2 main2_1 (.CLOCK(clock), .CLEAR(or_1_out), .CONTROL(1'b0), .Q3(q3), .Q2(q2), .Q1(q1), .Q0(q0));
  and_using_nand and_using_nand_1 (.A(p1), .B(not_1_out), .S(and_using_nand_1_s));
  and_using_nand and_using_nand_2 (.A(n3_input_and_using_nand_1_s), .B(clock), .S(and_using_nand_2_s));
  not not_1 (not_1_out, p0);
  _3_input_and_using_nand u_3_input_and_using_nand_1 (.A(q3), .B(q0), .C(1'b1), .S(n3_input_and_using_nand_1_s));
endmodule

module mod_6_counter (
  input  CONTROL,
  input  CLOCK,
  input  CLEAR,
  output Q2,
  output Q1,
  output Q0
);

  wire j_k_ff_1_qn, j_k_ff_2_qn, j_k_ff_3_qn, n3_input_and_using_nand_1_s, n3_input_and_using_nand_2_s,
       n3_input_and_using_nand_3_s, n3_input_and_using_nand_4_s, n7segment_decoder_1_a_2,
       n7segment_decoder_1_b_2, n7segment_decoder_1_c_2, n7segment_decoder_1_d_2, n7segment_decoder_1_e,
       n7segment_decoder_1_f, n7segment_decoder_1_g, not_using_nand_1_a_prime, or_using_nand_1_s,
       or_using_nand_2_s, xor_using_nand_1_s;

  not_using_nand not_using_nand_1 (.A(CONTROL), .A_prime(not_using_nand_1_a_prime));
  J_K_Flip_Flop #(.trigger("falling")) j_k_ff_1 (
    .J(1'b1), .clk(CLOCK), .K(1'b1), .Q(Q0), .Qn(j_k_ff_1_qn), .reset(CLEAR));  // open: preset, en
  _3_input_and_using_nand u_3_input_and_using_nand_1 (
    .A(not_using_nand_1_a_prime), .B(Q0), .C(j_k_ff_3_qn), .S(n3_input_and_using_nand_1_s));
  _3_input_and_using_nand u_3_input_and_using_nand_2 (
    .A(j_k_ff_1_qn), .B(Q2), .C(CONTROL), .S(n3_input_and_using_nand_2_s));
  or_using_nand or_using_nand_1 (
    .A(n3_input_and_using_nand_2_s), .B(n3_input_and_using_nand_1_s), .S(or_using_nand_1_s));
  J_K_Flip_Flop #(.trigger("falling")) j_k_ff_2 (
    .J(or_using_nand_1_s), .clk(CLOCK), .K(xor_using_nand_1_s), .Q(Q1), .Qn(j_k_ff_2_qn), .reset(CLEAR));  // open: preset, en
  _3_input_and_using_nand u_3_input_and_using_nand_3 (
    .A(j_k_ff_2_qn), .B(j_k_ff_1_qn), .C(CONTROL), .S(n3_input_and_using_nand_3_s));
  _3_input_and_using_nand u_3_input_and_using_nand_4 (
    .A(not_using_nand_1_a_prime), .B(Q0), .C(Q1), .S(n3_input_and_using_nand_4_s));
  or_using_nand or_using_nand_2 (
    .A(n3_input_and_using_nand_3_s), .B(n3_input_and_using_nand_4_s), .S(or_using_nand_2_s));
  xor_using_nand xor_using_nand_1 (.A(Q0), .B(CONTROL), .S(xor_using_nand_1_s));
  J_K_Flip_Flop #(.trigger("falling")) j_k_ff_3 (
    .J(or_using_nand_2_s), .clk(CLOCK), .K(xor_using_nand_1_s), .Q(Q2), .Qn(j_k_ff_3_qn), .reset(CLEAR));  // open: preset, en
  _7segment_decoder u_7segment_decoder_1 (
    .D(1'b0), .C(Q2), .B(Q1), .A(Q0), .a_2(n7segment_decoder_1_a_2), .b_2(n7segment_decoder_1_b_2),
    .c_2(n7segment_decoder_1_c_2), .d_2(n7segment_decoder_1_d_2), .e(n7segment_decoder_1_e),
    .f(n7segment_decoder_1_f), .g(n7segment_decoder_1_g));
  _7_Segment_Display u_7_segment_display_1 (
    .g(n7segment_decoder_1_g), .f(n7segment_decoder_1_f), .a(n7segment_decoder_1_a_2),
    .b(n7segment_decoder_1_b_2), .e(n7segment_decoder_1_e), .d(n7segment_decoder_1_d_2),
    .c(n7segment_decoder_1_c_2));  // open: dp

  // Notes on the sheet:
  //   UP (0) / DOWN (1)
endmodule

module _7segment_decoder (
  input  D,
  input  C,
  input  B,
  input  A,
  output a_2,
  output b_2,
  output c_2,
  output d_2,
  output e,
  output f,
  output g
);

  wire nand_1_out, nand_2_out, nand_3_out, nand_4_out, nand_5_out, nand_6_out, nand_7_out, nand_8_out,
       nand_9_out, nand_10_out, nand_11_out, nand_12_out, nand_13_out, nand_14_out, nand_15_out, nand_16_out,
       nand_17_out, nand_18_out, nand_19_out, nand_20_out, nand_21_out, nand_22_out, nand_23_out,
       nand_24_out, nand_25_out, nand_26_out, nand_27_out, nand_28_out, nand_29_out, nand_30_out,
       nand_31_out, nand_32_out, nand_33_out, nand_34_out, nand_35_out, nand_36_out, nand_37_out,
       nand_38_out, nand_39_out, nand_40_out, nand_41_out, nand_42_out, nand_43_out, nand_44_out,
       nand_45_out, nand_46_out, nand_47_out, nand_48_out, nand_49_out, nand_50_out, nand_51_out,
       nand_52_out, nand_53_out, nand_54_out, nand_55_out, nand_56_out, nand_57_out, nand_58_out,
       nand_59_out, nand_60_out, nand_61_out, nand_62_out, nand_63_out, nand_64_out, nand_65_out,
       nand_66_out, nand_67_out, nand_68_out, nand_69_out, nand_70_out, nand_71_out, nand_72_out,
       nand_73_out, nand_74_out, nand_75_out, nand_76_out, nand_77_out, nand_78_out, nand_79_out,
       nand_80_out, nand_81_out, nand_82_out, nand_83_out, nand_84_out, nand_85_out, nand_86_out,
       nand_87_out, nand_88_out, nand_89_out, nand_90_out, nand_91_out, nand_92_out, nand_93_out,
       nand_94_out, nand_95_out, nand_96_out, nand_97_out, nand_98_out, nand_99_out, nand_100_out,
       nand_101_out, nand_102_out, nand_103_out, nand_104_out, nand_106_out, nand_107_out, nand_108_out,
       nand_109_out, nand_110_out, nand_111_out, nand_112_out, nand_113_out, nand_114_out, nand_115_out,
       nand_116_out, nand_117_out, nand_118_out, nand_119_out, nand_120_out, nand_121_out, nand_122_out,
       nand_123_out, nand_124_out, nand_125_out, nand_126_out, nand_127_out, nand_128_out, nand_129_out,
       nand_130_out, nand_131_out, nand_132_out, nand_133_out, nand_134_out, nand_136_out, nand_137_out,
       nand_138_out, nand_139_out, nand_141_out, nand_142_out, nand_143_out, nand_144_out, nand_145_out,
       nand_146_out, nand_147_out, nand_148_out;

  nand nand_1 (nand_1_out, C, C);
  nand nand_2 (nand_2_out, D, D);
  nand nand_3 (nand_3_out, B, B);
  nand nand_4 (nand_4_out, D, D);
  nand nand_5 (nand_5_out, B, B);
  nand nand_6 (nand_6_out, D, D);
  nand nand_7 (nand_7_out, D, D);
  nand nand_8 (nand_8_out, C, C);
  nand nand_9 (nand_9_out, C, C);
  nand nand_10 (nand_10_out, C, C);
  nand nand_11 (nand_11_out, A, A);
  nand nand_12 (nand_12_out, A, A);
  nand nand_13 (nand_13_out, D, D);
  nand nand_14 (nand_14_out, C, C);
  nand nand_15 (nand_15_out, A, A);
  nand nand_16 (nand_16_out, D, D);
  nand nand_17 (nand_17_out, D, nand_1_out);
  nand nand_18 (nand_18_out, nand_2_out, nand_3_out);
  nand nand_19 (nand_19_out, nand_4_out, nand_5_out);
  nand nand_20 (nand_20_out, nand_6_out, A);
  nand nand_21 (nand_21_out, nand_7_out, nand_8_out);
  nand nand_22 (nand_22_out, nand_9_out, B);
  nand nand_23 (nand_23_out, nand_10_out, nand_11_out);
  nand nand_24 (nand_24_out, B, nand_12_out);
  nand nand_25 (nand_25_out, D, B);
  nand nand_26 (nand_26_out, D, C);
  nand nand_27 (nand_27_out, nand_13_out, C);
  nand nand_28 (nand_28_out, nand_14_out, B);
  nand nand_29 (nand_29_out, B, nand_15_out);
  nand nand_30 (nand_30_out, nand_16_out, C);
  nand nand_31 (nand_31_out, C, C);
  nand nand_32 (nand_32_out, A, A);
  nand nand_33 (nand_33_out, D, D);
  nand nand_34 (nand_34_out, D, D);
  nand nand_35 (nand_35_out, nand_17_out, nand_17_out);
  nand nand_36 (nand_36_out, B, B);
  nand nand_37 (nand_37_out, D, D);
  nand nand_38 (nand_38_out, C, C);
  nand nand_39 (nand_39_out, nand_18_out, nand_18_out);
  nand nand_40 (nand_40_out, A, A);
  nand nand_41 (nand_41_out, D, D);
  nand nand_42 (nand_42_out, B, B);
  nand nand_43 (nand_43_out, nand_19_out, nand_20_out);
  nand nand_44 (nand_44_out, B, B);
  nand nand_45 (nand_45_out, D, D);
  nand nand_46 (nand_46_out, C, C);
  nand nand_47 (nand_47_out, nand_21_out, nand_21_out);
  nand nand_48 (nand_48_out, A, A);
  nand nand_49 (nand_49_out, nand_22_out, nand_22_out);
  nand nand_50 (nand_50_out, B, B);
  nand nand_51 (nand_51_out, B, B);
  nand nand_52 (nand_52_out, nand_23_out, nand_24_out);
  nand nand_53 (nand_53_out, nand_25_out, nand_26_out);
  nand nand_54 (nand_54_out, B, B);
  nand nand_55 (nand_55_out, A, A);
  nand nand_56 (nand_56_out, nand_27_out, nand_27_out);
  nand nand_57 (nand_57_out, B, B);
  nand nand_58 (nand_58_out, nand_28_out, nand_29_out);
  nand nand_59 (nand_59_out, nand_30_out, nand_30_out);
  nand nand_60 (nand_60_out, B, B);
  nand nand_61 (nand_61_out, C, C);
  nand nand_62 (nand_62_out, nand_31_out, nand_32_out);
  nand nand_63 (nand_63_out, nand_33_out, B);
  nand nand_64 (nand_64_out, nand_34_out, C);
  nand nand_65 (nand_65_out, C, B);
  nand nand_66 (nand_66_out, nand_35_out, nand_36_out);
  nand nand_67 (nand_67_out, nand_37_out, nand_38_out);
  nand nand_68 (nand_68_out, nand_39_out, nand_40_out);
  nand nand_69 (nand_69_out, nand_41_out, B);
  nand nand_70 (nand_70_out, D, nand_42_out);
  nand nand_71 (nand_71_out, nand_43_out, nand_43_out);
  nand nand_72 (nand_72_out, nand_44_out, A);
  nand nand_73 (nand_73_out, nand_45_out, C);
  nand nand_74 (nand_74_out, D, nand_46_out);
  nand nand_75 (nand_75_out, nand_47_out, nand_48_out);
  nand nand_76 (nand_76_out, nand_49_out, A);
  nand nand_77 (nand_77_out, C, nand_50_out);
  nand nand_78 (nand_78_out, C, B);
  nand nand_79 (nand_79_out, D, nand_51_out);
  nand nand_80 (nand_80_out, nand_52_out, nand_52_out);
  nand nand_81 (nand_81_out, nand_53_out, nand_53_out);
  nand nand_82 (nand_82_out, nand_54_out, nand_55_out);
  nand nand_83 (nand_83_out, nand_56_out, nand_57_out);
  nand nand_84 (nand_84_out, nand_58_out, nand_58_out);
  nand nand_85 (nand_85_out, nand_59_out, nand_60_out);
  nand nand_86 (nand_86_out, D, nand_61_out);
  nand nand_87 (nand_87_out, D, A);
  nand nand_88 (nand_88_out, nand_62_out, nand_63_out);
  nand nand_89 (nand_89_out, nand_64_out, nand_64_out);
  nand nand_90 (nand_90_out, nand_65_out, nand_66_out);
  nand nand_91 (nand_91_out, A, A);
  nand nand_92 (nand_92_out, nand_67_out, nand_68_out);
  nand nand_93 (nand_93_out, C, C);
  nand nand_94 (nand_94_out, A, A);
  nand nand_95 (nand_95_out, nand_69_out, nand_69_out);
  nand nand_96 (nand_96_out, nand_70_out, nand_70_out);
  nand nand_97 (nand_97_out, nand_71_out, nand_72_out);
  nand nand_98 (nand_98_out, nand_73_out, nand_74_out);
  nand nand_99 (nand_99_out, nand_75_out, nand_76_out);
  nand nand_100 (nand_100_out, nand_77_out, nand_77_out);
  nand nand_101 (nand_101_out, nand_78_out, nand_78_out);
  nand nand_102 (nand_102_out, A, A);
  nand nand_103 (nand_103_out, nand_79_out, nand_79_out);
  nand nand_104 (nand_104_out, A, A);
  nand nand_105 (e, nand_80_out, nand_81_out);
  nand nand_106 (nand_106_out, nand_82_out, nand_83_out);
  nand nand_107 (nand_107_out, A, A);
  nand nand_108 (nand_108_out, C, C);
  nand nand_109 (nand_109_out, nand_84_out, nand_85_out);
  nand nand_110 (nand_110_out, nand_86_out, nand_87_out);
  nand nand_111 (nand_111_out, nand_88_out, nand_88_out);
  nand nand_112 (nand_112_out, nand_89_out, A);
  nand nand_113 (nand_113_out, nand_90_out, nand_90_out);
  nand nand_114 (nand_114_out, D, nand_91_out);
  nand nand_115 (nand_115_out, nand_92_out, nand_92_out);
  nand nand_116 (nand_116_out, nand_93_out, nand_94_out);
  nand nand_117 (nand_117_out, nand_95_out, A);
  nand nand_118 (nand_118_out, nand_96_out, A);
  nand nand_119 (nand_119_out, nand_97_out, nand_97_out);
  nand nand_120 (nand_120_out, nand_98_out, nand_98_out);
  nand nand_121 (nand_121_out, nand_99_out, nand_99_out);
  nand nand_122 (nand_122_out, nand_100_out, A);
  nand nand_123 (nand_123_out, nand_101_out, nand_102_out);
  nand nand_124 (nand_124_out, nand_103_out, nand_104_out);
  nand nand_125 (nand_125_out, nand_106_out, nand_106_out);
  nand nand_126 (nand_126_out, C, nand_107_out);
  nand nand_127 (nand_127_out, D, nand_108_out);
  nand nand_128 (nand_128_out, D, B);
  nand nand_129 (nand_129_out, nand_109_out, nand_109_out);
  nand nand_130 (nand_130_out, nand_110_out, nand_110_out);
  nand nand_131 (nand_131_out, nand_111_out, nand_112_out);
  nand nand_132 (nand_132_out, nand_113_out, nand_114_out);
  nand nand_133 (nand_133_out, nand_115_out, nand_116_out);
  nand nand_134 (nand_134_out, nand_117_out, nand_118_out);
  nand nand_135 (c_2, nand_119_out, nand_120_out);
  nand nand_136 (nand_136_out, nand_121_out, nand_122_out);
  nand nand_137 (nand_137_out, nand_123_out, nand_124_out);
  nand nand_138 (nand_138_out, nand_125_out, nand_126_out);
  nand nand_139 (nand_139_out, nand_127_out, nand_128_out);
  nand nand_140 (g, nand_129_out, nand_130_out);
  nand nand_141 (nand_141_out, nand_131_out, nand_131_out);
  nand nand_142 (nand_142_out, nand_132_out, nand_132_out);
  nand nand_143 (nand_143_out, nand_133_out, nand_133_out);
  nand nand_144 (nand_144_out, nand_134_out, nand_134_out);
  nand nand_145 (nand_145_out, nand_136_out, nand_136_out);
  nand nand_146 (nand_146_out, nand_137_out, nand_137_out);
  nand nand_147 (nand_147_out, nand_138_out, nand_138_out);
  nand nand_148 (nand_148_out, nand_139_out, nand_139_out);
  nand nand_149 (a_2, nand_141_out, nand_142_out);
  nand nand_150 (b_2, nand_143_out, nand_144_out);
  nand nand_151 (d_2, nand_145_out, nand_146_out);
  nand nand_152 (f, nand_147_out, nand_148_out);
endmodule

// CONDITIONAL
module switch (
  input  I0,
  input  I1,
  input  CONTROL,
  output Q
);

  wire nand_1_out, nand_2_out, not_using_nand_1_a_prime, not_using_nand_2_a_prime;

  not_using_nand not_using_nand_1 (.A(not_using_nand_2_a_prime), .A_prime(not_using_nand_1_a_prime));
  not_using_nand not_using_nand_2 (.A(CONTROL), .A_prime(not_using_nand_2_a_prime));
  nand nand_1 (nand_1_out, I0, not_using_nand_1_a_prime);
  nand nand_2 (nand_2_out, not_using_nand_2_a_prime, I1);
  nand nand_3 (Q, nand_1_out, nand_2_out);
endmodule

module mini_circ (
  input  Q2,
  input  Q3,
  input  Q0_prime,
  output out_4
);

  wire or_using_nand_1_s;

  or_using_nand or_using_nand_1 (.A(Q2), .B(Q3), .S(or_using_nand_1_s));
  and_using_nand and_using_nand_1 (.A(or_using_nand_1_s), .B(Q0_prime), .S(out_4));
endmodule

// XOR
module xor_using_nand (
  input  A,
  input  B,
  output S
);

  wire nand_1_out, nand_2_out, nand_3_out;

  nand nand_1 (nand_1_out, A, B);
  nand nand_2 (nand_2_out, A, nand_1_out);
  nand nand_3 (nand_3_out, nand_1_out, B);
  nand nand_4 (S, nand_2_out, nand_3_out);

  // Notes on the sheet:
  //   XOR USING NAND
endmodule

// OR
module or_using_nand (
  input  A,
  input  B,
  output S
);

  wire nand_1_out, nand_2_out;

  nand nand_1 (nand_1_out, A, A);
  nand nand_2 (nand_2_out, B, B);
  nand nand_3 (S, nand_1_out, nand_2_out);

  // Notes on the sheet:
  //   OR USING NAND
endmodule

// AND
module and_using_nand (
  input  A,
  input  B,
  output S
);

  wire nand_1_out;

  nand nand_1 (nand_1_out, A, B);
  nand nand_2 (S, nand_1_out, nand_1_out);

  // Notes on the sheet:
  //   AND USING NAND
endmodule

// NOT
module not_using_nand (
  input  A,
  output A_prime
);

  nand nand_1 (A_prime, A, A);

  // Notes on the sheet:
  //   NOT USING NAND
endmodule

// AND3
module _3_input_and_using_nand (
  input  A,
  input  B,
  input  C,
  output S
);

  wire nand_1_out, nand_2_out, nand_3_out;

  nand nand_1 (nand_1_out, A, B);
  nand nand_2 (nand_2_out, nand_1_out, nand_1_out);
  nand nand_3 (nand_3_out, nand_2_out, C);
  nand nand_4 (S, nand_3_out, nand_3_out);

  // Notes on the sheet:
  //   3 INPUT AND USING NAND
endmodule

module main (
  input  control,
  input  units,
  input  i3,
  input  i0,
  input  clock,
  output out_6
);

  wire and_using_nand_1_s, n3_input_and_using_nand_1_s;

  _3_input_and_using_nand u_3_input_and_using_nand_1 (.A(control), .B(i3), .C(i0), .S(n3_input_and_using_nand_1_s));
  and_using_nand and_using_nand_1 (.A(units), .B(n3_input_and_using_nand_1_s), .S(and_using_nand_1_s));
  and_using_nand and_using_nand_2 (.A(and_using_nand_1_s), .B(clock), .S(out_6));
endmodule

module _0_59__temp (
  input  CLOCK,
  input  CONTROL,
  input  CLEAR,
  output q3,
  output q2,
  output q1,
  output q0,
  output p2,
  output p1,
  output p0
);

  wire and_1_out, and_using_nand_1_s, and_using_nand_2_s, n3_input_and_using_nand_1_s, not_1_out, not_2_out,
       not_3_out, not_4_out, not_using_nand_1_a_prime, or_using_nand_1_s;

  main2 main2_1 (.CLOCK(CLOCK), .CLEAR(CLEAR), .CONTROL(CONTROL), .Q3(q3), .Q2(q2), .Q1(q1), .Q0(q0));
  not_using_nand not_using_nand_1 (.A(CONTROL), .A_prime(not_using_nand_1_a_prime));
  _3_input_and_using_nand u_3_input_and_using_nand_1 (
    .A(not_using_nand_1_a_prime), .B(q3), .C(q0), .S(n3_input_and_using_nand_1_s));
  or_using_nand or_using_nand_1 (.A(and_using_nand_2_s), .B(n3_input_and_using_nand_1_s), .S(or_using_nand_1_s));
  and_using_nand and_using_nand_1 (.A(or_using_nand_1_s), .B(CLOCK), .S(and_using_nand_1_s));
  mod_6_counter mod_6_counter_1 (
    .CONTROL(CONTROL), .CLOCK(and_using_nand_1_s), .CLEAR(CLEAR), .Q2(p2), .Q1(p1), .Q0(p0));
  not not_1 (not_1_out, q0);
  not not_2 (not_2_out, q3);
  not not_3 (not_3_out, q1);
  not not_4 (not_4_out, q2);
  and and_1 (and_1_out, not_1_out, not_2_out, not_3_out, not_4_out);
  and_using_nand and_using_nand_2 (.A(and_1_out), .B(CONTROL), .S(and_using_nand_2_s));

  // Notes on the sheet:
  //   UP (0) / DOWN (1)
endmodule

module mod_3 (
  input  clock,
  input  clear,
  output q1,
  output q0
);

  wire j_k_ff_2_qn;

  J_K_Flip_Flop #(.trigger("falling")) j_k_ff_1 (
    .J(j_k_ff_2_qn), .clk(clock), .K(1'b1), .Q(q0), .reset(clear));  // open: Qn, preset, en
  J_K_Flip_Flop #(.trigger("falling")) j_k_ff_2 (
    .J(q0), .clk(clock), .K(1'b1), .Q(q1), .Qn(j_k_ff_2_qn), .reset(clear));  // open: preset, en

  // Notes on the sheet:
  //   MOD 3 COUNTER
  //   (without parallel loading)
endmodule

module mod_6 (
  input  CLOCK,
  input  CLEAR,
  output Q2,
  output Q1,
  output Q0
);

  wire and_using_nand_1_s, and_using_nand_2_s, j_k_ff_3_qn, n7segment_decoder_1_a_2, n7segment_decoder_1_b_2,
       n7segment_decoder_1_c_2, n7segment_decoder_1_d_2, n7segment_decoder_1_e, n7segment_decoder_1_f,
       n7segment_decoder_1_g;

  J_K_Flip_Flop #(.trigger("falling")) j_k_ff_1 (
    .J(1'b1), .clk(CLOCK), .K(1'b1), .Q(Q0), .reset(CLEAR));  // open: Qn, preset, en
  and_using_nand and_using_nand_1 (.A(Q0), .B(j_k_ff_3_qn), .S(and_using_nand_1_s));
  J_K_Flip_Flop #(.trigger("falling")) j_k_ff_2 (
    .J(and_using_nand_1_s), .clk(CLOCK), .K(Q0), .Q(Q1), .reset(CLEAR));  // open: Qn, preset, en
  and_using_nand and_using_nand_2 (.A(Q0), .B(Q1), .S(and_using_nand_2_s));
  J_K_Flip_Flop #(.trigger("falling")) j_k_ff_3 (
    .J(and_using_nand_2_s), .clk(CLOCK), .K(Q0), .Q(Q2), .Qn(j_k_ff_3_qn), .reset(CLEAR));  // open: preset, en
  _7segment_decoder u_7segment_decoder_1 (
    .D(1'b0), .C(Q2), .B(Q1), .A(Q0), .a_2(n7segment_decoder_1_a_2), .b_2(n7segment_decoder_1_b_2),
    .c_2(n7segment_decoder_1_c_2), .d_2(n7segment_decoder_1_d_2), .e(n7segment_decoder_1_e),
    .f(n7segment_decoder_1_f), .g(n7segment_decoder_1_g));
  _7_Segment_Display u_7_segment_display_1 (
    .g(n7segment_decoder_1_g), .f(n7segment_decoder_1_f), .a(n7segment_decoder_1_a_2),
    .b(n7segment_decoder_1_b_2), .e(n7segment_decoder_1_e), .d(n7segment_decoder_1_d_2),
    .c(n7segment_decoder_1_c_2));  // open: dp

  // Notes on the sheet:
  //   MOD 6 COUNTER
  //   (without parallel loading)
endmodule
