// Logisim project traffic.circ as structural Verilog: 15 circuits, main circuit main
module main (
  input  CLEAR,
  input  [3:0] in_2,
  input  [3:0] in_3,
  input  [3:0] in_4,
  input  [3:0] in_5,
  input  [3:0] in_6,
  input  [3:0] in_7,
  input  count,
  input  load
);

  wire and_1_out, and_2_out, demultiplexer_1_out0, demultiplexer_1_out1, demultiplexer_1_out2,
       demultiplexer_1_out3, hours_combination_1_out_3, mod_3_1_q0, mod_3_1_q1, multiplexer_1_out, not_1_out,
       not_2_out, or_1_out, or_2_out, or_3_out, or_4_out, signal_1_right, signal_1_stop, signal_1_straight,
       signal_2_right, signal_2_stop, signal_2_straight, signal_3_left, signal_3_right, signal_3_stop,
       signal_3_straight, signal_4_right, signal_4_stop, signal_4_straight, START_out, timer60_1_clock_out,
       timer_1_clock_out;
  wire [1:0] mod_4_1_q0;
  wire [3:0] clock_1_hh, clock_1_mm, clock_1_out_11, clock_1_out_12, clock_1_out_14, clock_1_out_16,
       timer60_1_mod3, timer60_1_mod10, timer_1_mod3, timer_1_mod10;

  Clock START (.out(START_out));
  mod_3 mod_3_1 (.CLEAR(and_1_out), .CLOCK(multiplexer_1_out), .q0(mod_3_1_q0), .q1(mod_3_1_q1));
  Hex_Digit_Display hex_digit_display_1 (.value(timer60_1_mod3));  // open: dp
  Hex_Digit_Display hex_digit_display_2 (.value(timer_1_mod3));  // open: dp
  not not_1 (not_1_out, mod_3_1_q1);
  not not_2 (not_2_out, mod_3_1_q0);
  and and_1 (and_1_out, mod_3_1_q1, not_2_out);
  Hex_Digit_Display hex_digit_display_3 (.value(timer60_1_mod10));  // open: dp
  timer60 timer60_1 (
    .CLOCK(START_out), .mod3(timer60_1_mod3), .mod10(timer60_1_mod10), .clock_out(timer60_1_clock_out));  // open: CLEAR
  Hex_Digit_Display hex_digit_display_4 (.value(timer_1_mod10));  // open: dp
  timer timer_1 (
    .CLOCK(START_out), .CLEAR(CLEAR), .mod3(timer_1_mod3), .mod10(timer_1_mod10),
    .clock_out(timer_1_clock_out));
  and and_2 (and_2_out, mod_3_1_q0, not_1_out);
  mod_4 mod_4_1 (.CLOCK(and_2_out), .Q1(mod_4_1_q0[1]), .Q0(mod_4_1_q0[0]));  // open: CLEAR
  Multiplexer #(.enable("false")) multiplexer_1 (
    .in0(timer_1_clock_out), .in1(timer60_1_clock_out), .out(multiplexer_1_out),
    .sel(hours_combination_1_out_3));
  Demultiplexer #(.select(2), .enable("false")) demultiplexer_1 (
    .out0(demultiplexer_1_out0), .out1(demultiplexer_1_out1), .out2(demultiplexer_1_out2),
    .out3(demultiplexer_1_out3), .in(START_out), .sel(mod_4_1_q0));
  or or_1 (or_1_out, demultiplexer_1_out0, demultiplexer_1_out1);
  LED led_1 (.in(signal_1_right));
  LED led_2 (.in(signal_1_straight));
  LED led_3 (.in(signal_1_stop));
  LED led_4 (.in(or_2_out));
  signal signal_1 (
    .CLOCK(demultiplexer_1_out3), .CLEAR(CLEAR), .select(hours_combination_1_out_3), .stop(signal_1_stop),
    .straight(signal_1_straight), .right(signal_1_right));  // open: left
  or or_2 (or_2_out, demultiplexer_1_out3, demultiplexer_1_out0);
  hours_combination hours_combination_1 (
    .decade(clock_1_out_14), .mod_4(clock_1_hh), .out_3(hours_combination_1_out_3));
  LED led_5 (.in(or_1_out));
  LED led_6 (.in(signal_2_straight));
  LED led_7 (.in(signal_2_stop));
  signal signal_2 (
    .CLOCK(demultiplexer_1_out0), .CLEAR(CLEAR), .select(hours_combination_1_out_3), .stop(signal_2_stop),
    .straight(signal_2_straight), .right(signal_2_right));  // open: left
  LED led_8 (.in(signal_2_right));
  LED led_9 (.in(signal_4_right));
  signal signal_3 (
    .CLOCK(demultiplexer_1_out1), .CLEAR(CLEAR), .select(hours_combination_1_out_3), .left(signal_3_left),
    .stop(signal_3_stop), .straight(signal_3_straight), .right(signal_3_right));
  signal signal_4 (
    .CLOCK(demultiplexer_1_out2), .CLEAR(CLEAR), .select(hours_combination_1_out_3), .stop(signal_4_stop),
    .straight(signal_4_straight), .right(signal_4_right));  // open: left
  LED led_10 (.in(signal_4_stop));
  LED led_11 (.in(or_4_out));
  LED led_12 (.in(signal_4_straight));
  or or_3 (or_3_out, demultiplexer_1_out2, demultiplexer_1_out1);
  LED led_13 (.in(or_3_out));
  LED led_14 (.in(signal_3_stop));
  LED led_15 (.in(signal_3_straight));
  LED led_16 (.in(signal_3_right));
  or or_4 (or_4_out, demultiplexer_1_out2, demultiplexer_1_out3);
  Hex_Digit_Display hex_digit_display_5 (.value(clock_1_hh));  // open: dp
  clock clock_1 (
    .UP_COUNT(count), .PARALLEL_LOAD(load), .in_6(in_2), .in_4(in_3), .in_5(in_4), .clear(CLEAR),
    .in_2(in_5), .in_1(in_6), .clock(START_out), .in_3(in_7), .HH(clock_1_hh), .out_14(clock_1_out_14),
    .MM(clock_1_mm), .out_16(clock_1_out_16), .out_11(clock_1_out_11), .out_12(clock_1_out_12));
  Hex_Digit_Display hex_digit_display_6 (.value(clock_1_out_14));  // open: dp
  Hex_Digit_Display hex_digit_display_7 (.value(clock_1_mm));  // open: dp
  Hex_Digit_Display hex_digit_display_8 (.value(clock_1_out_11));  // open: dp
  Hex_Digit_Display hex_digit_display_9 (.value(clock_1_out_16));  // open: dp
  Hex_Digit_Display hex_digit_display_10 (.value(clock_1_out_12));  // open: dp

  // Notes on the sheet:
  //   60s timer
  //   30s timer
  //   right
  //   straight
  //   WEST
  //   stop
  //   left
  //   straight
  //   stop
  //   left
  //   right
  //   NORTH
  //   SOUTH
  //   right
  //   EAST
  //   left
  //   stop
  //   straight
  //   left
  //   stop
  //   straight
  //   right
  //   HH
  //   MM
  //   Traffic Signal
  //   SS
endmodule

module mod_4 (
  input  CLOCK,
  input  CLEAR,
  output Q1,
  output Q0
);

  J_K_Flip_Flop #(.trigger("falling")) j_k_ff_1 (
    .J(1'b1), .clk(CLOCK), .K(1'b1), .Q(Q0), .reset(CLEAR));  // open: Qn, preset, en
  J_K_Flip_Flop #(.trigger("falling")) j_k_ff_2 (
    .J(Q0), .clk(CLOCK), .K(Q0), .Q(Q1), .reset(CLEAR));  // open: Qn, preset, en
endmodule

module signal (
  input  CLOCK,
  input  CLEAR,
  input  select,
  output left,
  output stop,
  output straight,
  output right
);

  wire multiplexer_1_out, not_1_out, timer60_1_clock_out, timer_1_clock_out;

  not not_1 (not_1_out, CLOCK);
  or or_1 (left, not_1_out, CLOCK);
  timer timer_1 (.CLOCK(CLOCK), .CLEAR(CLEAR), .clock_out(timer_1_clock_out));  // open: mod3, mod10
  timer60 timer60_1 (.CLOCK(CLOCK), .CLEAR(CLEAR), .clock_out(timer60_1_clock_out));  // open: mod3, mod10
  Multiplexer #(.enable("false")) multiplexer_1 (
    .in0(timer_1_clock_out), .in1(timer60_1_clock_out), .out(multiplexer_1_out), .sel(select));
  not not_2 (stop, right);
  mod_2 mod_2_1 (.clock(multiplexer_1_out), .clear(CLEAR), .q0(right));

  assign straight = right;

  // Notes on the sheet:
  //   signalling circuit
endmodule

module decade (
  input  COUNT,
  input  LOAD,
  input  i0,
  input  i1,
  input  i2,
  input  i3,
  input  CLEAR,
  input  CLOCK,
  output q0,
  output q1,
  output q2,
  output q3
);

  wire and_1_out, and_2_out, and_3_out, and_4_out, and_5_out, and_6_out, and_7_out, and_8_out, and_9_out,
       and_10_out, and_11_out, and_12_out, and_13_out, not_1_out, not_2_out, not_3_out, not_4_out, not_5_out,
       or_1_out, or_2_out, or_3_out, or_4_out, or_5_out, or_6_out, or_7_out, or_8_out, or_9_out;

  not not_1 (not_1_out, i0);
  not not_2 (not_2_out, i1);
  not not_3 (not_3_out, i2);
  not not_4 (not_4_out, i3);
  and and_1 (and_1_out, COUNT, not_5_out);
  not not_5 (not_5_out, LOAD);
  and and_2 (and_2_out, i0, LOAD);
  and and_3 (and_3_out, not_1_out, LOAD);
  and and_4 (and_4_out, i1, LOAD);
  and and_5 (and_5_out, LOAD, not_2_out);
  and and_6 (and_6_out, i2, LOAD);
  and and_7 (and_7_out, not_3_out, LOAD);
  and and_8 (and_8_out, i3, LOAD);
  and and_9 (and_9_out, not_4_out, LOAD);
  and and_10 (and_10_out, q1, q3);
  and and_11 (and_11_out, q0, and_1_out);
  and and_12 (and_12_out, and_1_out, q0, q1);
  and and_13 (and_13_out, q2, q1, q0, and_1_out);
  or or_1 (or_1_out, and_10_out, CLEAR);
  or or_2 (or_2_out, and_2_out, and_1_out);
  or or_3 (or_3_out, and_3_out, and_1_out);
  or or_4 (or_4_out, and_4_out, and_11_out);
  or or_5 (or_5_out, and_11_out, and_5_out);
  or or_6 (or_6_out, and_6_out, and_12_out);
  or or_7 (or_7_out, and_12_out, and_7_out);
  or or_8 (or_8_out, and_8_out, and_13_out);
  or or_9 (or_9_out, and_13_out, and_9_out);
  J_K_Flip_Flop #(.trigger("falling")) j_k_ff_1 (
    .J(or_2_out), .clk(CLOCK), .K(or_3_out), .Q(q0), .reset(or_1_out));  // open: Qn, preset, en
  J_K_Flip_Flop #(.trigger("falling")) j_k_ff_2 (
    .J(or_4_out), .clk(CLOCK), .K(or_5_out), .Q(q1), .reset(or_1_out));  // open: Qn, preset, en
  J_K_Flip_Flop #(.trigger("falling")) j_k_ff_3 (
    .J(or_6_out), .clk(CLOCK), .K(or_7_out), .Q(q2), .reset(or_1_out));  // open: Qn, preset, en
  J_K_Flip_Flop #(.trigger("falling")) j_k_ff_4 (
    .J(or_8_out), .clk(CLOCK), .K(or_9_out), .Q(q3), .reset(or_1_out));  // open: Qn, preset, en

  // Notes on the sheet:
  //   DECADE COUNTER
  //   (with parallel loading)
endmodule

module mod_3 (
  input  CLEAR,
  input  CLOCK,
  output q0,
  output q1
);

  wire and_1_out, and_2_out, and_3_out, and_4_out, and_5_out, and_6_out, and_7_out, and_8_out, and_9_out,
       and_10_out, and_11_out, and_12_out, and_13_out, j_k_ff_3_q, j_k_ff_4_q, not_1_out, not_2_out,
       not_3_out, not_4_out, not_5_out, or_1_out, or_2_out, or_3_out, or_4_out, or_5_out, or_6_out, or_7_out,
       or_8_out, or_9_out;

  not not_1 (not_1_out, 1'b0);
  not not_2 (not_2_out, 1'b0);
  not not_3 (not_3_out, 1'b0);
  not not_4 (not_4_out, 1'b0);
  and and_1 (and_1_out, 1'b1, not_5_out);
  not not_5 (not_5_out, 1'b0);
  and and_2 (and_2_out, 1'b0, 1'b0);
  and and_3 (and_3_out, not_1_out, 1'b0);
  and and_4 (and_4_out, 1'b0, 1'b0);
  and and_5 (and_5_out, 1'b0, not_2_out);
  and and_6 (and_6_out, 1'b0, 1'b0);
  and and_7 (and_7_out, not_3_out, 1'b0);
  and and_8 (and_8_out, 1'b0, 1'b0);
  and and_9 (and_9_out, not_4_out, 1'b0);
  and and_10 (and_10_out, q1, q0);
  and and_11 (and_11_out, q0, and_1_out);
  and and_12 (and_12_out, and_1_out, q0, q1);
  and and_13 (and_13_out, j_k_ff_3_q, q1, q0, and_1_out);
  or or_1 (or_1_out, and_10_out, CLEAR);
  or or_2 (or_2_out, and_2_out, and_1_out);
  or or_3 (or_3_out, and_3_out, and_1_out);
  or or_4 (or_4_out, and_4_out, and_11_out);
  or or_5 (or_5_out, and_11_out, and_5_out);
  or or_6 (or_6_out, and_6_out, and_12_out);
  or or_7 (or_7_out, and_12_out, and_7_out);
  or or_8 (or_8_out, and_8_out, and_13_out);
  or or_9 (or_9_out, and_13_out, and_9_out);
  J_K_Flip_Flop #(.trigger("falling")) j_k_ff_1 (
    .J(or_2_out), .clk(CLOCK), .K(or_3_out), .Q(q0), .reset(or_1_out));  // open: Qn, preset, en
  J_K_Flip_Flop #(.trigger("falling")) j_k_ff_2 (
    .J(or_4_out), .clk(CLOCK), .K(or_5_out), .Q(q1), .reset(or_1_out));  // open: Qn, preset, en
  J_K_Flip_Flop #(.trigger("falling")) j_k_ff_3 (
    .J(or_6_out), .clk(CLOCK), .K(or_7_out), .Q(j_k_ff_3_q), .reset(or_1_out));  // open: Qn, preset, en
  J_K_Flip_Flop #(.trigger("falling")) j_k_ff_4 (
    .J(or_8_out), .clk(CLOCK), .K(or_9_out), .Q(j_k_ff_4_q), .reset(or_1_out));  // open: Qn, preset, en
  // also tied to GND on the sheet: {j_k_ff_3_q, j_k_ff_4_q}

  // Notes on the sheet:
  //   MOD 3 COUNTER
  //   (with parallel loading)
endmodule

module mod_30 (
  input  CLOCK,
  input  CLEAR,
  output q0,
  output q1,
  output q2,
  output q3,
  output p0,
  output p1
);

  wire and_1_out, and_2_out, or_1_out;

  or or_1 (or_1_out, and_2_out, CLEAR);
  decade decade_1 (
    .COUNT(1'b1), .LOAD(1'b0), .i0(1'b0), .i1(1'b0), .i2(1'b0), .i3(1'b0), .CLEAR(or_1_out), .CLOCK(CLOCK),
    .q0(q0), .q1(q1), .q2(q2), .q3(q3));
  and and_1 (and_1_out, 1'b1, CLOCK, q3, q0);
  mod_3 mod_3_1 (.CLEAR(or_1_out), .CLOCK(and_1_out), .q0(p0), .q1(p1));
  and and_2 (and_2_out, q1, q3, p1, p0);

  // Notes on the sheet:
  //   MOD 30 COUNTER
endmodule

module timer (
  input  CLOCK,
  input  CLEAR,
  output clock_out,
  output [3:0] mod3,
  output [3:0] mod10
);

  mod_30 mod_30_1 (
    .CLOCK(CLOCK), .CLEAR(CLEAR), .q0(mod10[0]), .q1(mod10[1]), .q2(mod10[2]), .q3(mod10[3]), .p0(mod3[0]),
    .p1(mod3[1]));
  and and_1 (clock_out, mod10[1], mod10[3], mod3[0], mod3[1]);

  assign mod3[3:2] = 2'b00;

  // Notes on the sheet:
  //   timing circuit for 30s
endmodule

module mod_24 (
  input  I3,
  input  I2,
  input  I1,
  input  I0,
  input  COUNT,
  input  LOAD,
  input  CLOCK,
  input  CLEAR,
  input  I1_2,
  input  I0_2,
  output q0,
  output q1,
  output q2,
  output q3,
  output p0,
  output p1
);

  wire and_1_out, and_2_out, mod_3_1_q2, mod_3_1_q3, multiplexer_1_out, or_1_out;

  or or_1 (or_1_out, and_2_out, CLEAR);
  decade decade_1 (
    .COUNT(COUNT), .LOAD(LOAD), .i0(I0), .i1(I1), .i2(I2), .i3(I3), .CLEAR(or_1_out), .CLOCK(CLOCK), .q0(q0),
    .q1(q1), .q2(q2), .q3(q3));
  mod_3_2 mod_3_1 (
    .COUNT(COUNT), .LOAD(LOAD), .i0(I0_2), .i1(I1_2), .i2(1'b0), .i3(1'b0), .CLEAR(or_1_out),
    .CLOCK(multiplexer_1_out), .q0(p0), .q1(p1), .q2(mod_3_1_q2), .q3(mod_3_1_q3));
  and and_1 (and_1_out, COUNT, CLOCK, q3, q0);
  Multiplexer #(.enable("false")) multiplexer_1 (.in0(and_1_out), .in1(CLOCK), .out(multiplexer_1_out), .sel(LOAD));
  and and_2 (and_2_out, q2, p1);
  // also tied to GND on the sheet: {mod_3_1_q2, mod_3_1_q3}

  // Notes on the sheet:
  //   MOD 24 COUNTER
  //   (with parallel loading)
endmodule

module mod_3_2 (
  input  COUNT,
  input  LOAD,
  input  i0,
  input  i1,
  input  i2,
  input  i3,
  input  CLEAR,
  input  CLOCK,
  output q0,
  output q1,
  output q2,
  output q3
);

  wire and_1_out, and_2_out, and_3_out, and_4_out, and_5_out, and_6_out, and_7_out, and_8_out, and_9_out,
       and_10_out, and_11_out, and_12_out, and_13_out, not_1_out, not_2_out, not_3_out, not_4_out, not_5_out,
       or_1_out, or_2_out, or_3_out, or_4_out, or_5_out, or_6_out, or_7_out, or_8_out, or_9_out;

  not not_1 (not_1_out, i0);
  not not_2 (not_2_out, i1);
  not not_3 (not_3_out, i2);
  not not_4 (not_4_out, i3);
  and and_1 (and_1_out, COUNT, not_5_out);
  not not_5 (not_5_out, LOAD);
  and and_2 (and_2_out, i0, LOAD);
  and and_3 (and_3_out, not_1_out, LOAD);
  and and_4 (and_4_out, i1, LOAD);
  and and_5 (and_5_out, LOAD, not_2_out);
  and and_6 (and_6_out, i2, LOAD);
  and and_7 (and_7_out, not_3_out, LOAD);
  and and_8 (and_8_out, i3, LOAD);
  and and_9 (and_9_out, not_4_out, LOAD);
  and and_10 (and_10_out, q1, q0);
  and and_11 (and_11_out, q0, and_1_out);
  and and_12 (and_12_out, and_1_out, q0, q1);
  and and_13 (and_13_out, q2, q1, q0, and_1_out);
  or or_1 (or_1_out, and_10_out, CLEAR);
  or or_2 (or_2_out, and_2_out, and_1_out);
  or or_3 (or_3_out, and_3_out, and_1_out);
  or or_4 (or_4_out, and_4_out, and_11_out);
  or or_5 (or_5_out, and_11_out, and_5_out);
  or or_6 (or_6_out, and_6_out, and_12_out);
  or or_7 (or_7_out, and_12_out, and_7_out);
  or or_8 (or_8_out, and_8_out, and_13_out);
  or or_9 (or_9_out, and_13_out, and_9_out);
  J_K_Flip_Flop #(.trigger("falling")) j_k_ff_1 (
    .J(or_2_out), .clk(CLOCK), .K(or_3_out), .Q(q0), .reset(or_1_out));  // open: Qn, preset, en
  J_K_Flip_Flop #(.trigger("falling")) j_k_ff_2 (
    .J(or_4_out), .clk(CLOCK), .K(or_5_out), .Q(q1), .reset(or_1_out));  // open: Qn, preset, en
  J_K_Flip_Flop #(.trigger("falling")) j_k_ff_3 (
    .J(or_6_out), .clk(CLOCK), .K(or_7_out), .Q(q2), .reset(or_1_out));  // open: Qn, preset, en
  J_K_Flip_Flop #(.trigger("falling")) j_k_ff_4 (
    .J(or_8_out), .clk(CLOCK), .K(or_9_out), .Q(q3), .reset(or_1_out));  // open: Qn, preset, en

  // Notes on the sheet:
  //   MOD 3 COUNTER
  //   (with parallel loading)
endmodule

module mod_60 (
  input  I3,
  input  I2,
  input  I1,
  input  I0,
  input  COUNT,
  input  LOAD,
  input  CLOCK,
  input  CLEAR,
  input  I2_2,
  input  I1_2,
  input  I0_2,
  output q3,
  output q2,
  output q1,
  output q0,
  output p2,
  output p1,
  output p0
);

  wire and_1_out, multiplexer_1_out;

  decade decade_1 (
    .COUNT(COUNT), .LOAD(LOAD), .i0(I0), .i1(I1), .i2(I2), .i3(I3), .CLEAR(CLEAR), .CLOCK(CLOCK), .q0(q0),
    .q1(q1), .q2(q2), .q3(q3));
  and and_1 (and_1_out, COUNT, CLOCK, q3, q0);
  Multiplexer #(.enable("false")) multiplexer_1 (.in0(and_1_out), .in1(CLOCK), .out(multiplexer_1_out), .sel(LOAD));
  mod_6 mod_6_1 (
    .COUNT(COUNT), .LOAD(LOAD), .i0(I0_2), .i1(I1_2), .i2(I2_2), .i3(1'b0), .CLEAR(CLEAR),
    .CLOCK(multiplexer_1_out), .q0(p0), .q1(p1), .q2(p2));  // open: q3

  // Notes on the sheet:
  //   MOD 60 COUNTER
  //   (with parallel loading)
endmodule

module mod_6 (
  input  COUNT,
  input  LOAD,
  input  i0,
  input  i1,
  input  i2,
  input  i3,
  input  CLEAR,
  input  CLOCK,
  output q0,
  output q1,
  output q2,
  output q3
);

  wire and_1_out, and_2_out, and_3_out, and_4_out, and_5_out, and_6_out, and_7_out, and_8_out, and_9_out,
       and_10_out, and_11_out, and_12_out, and_13_out, not_1_out, not_2_out, not_3_out, not_4_out, not_5_out,
       or_1_out, or_2_out, or_3_out, or_4_out, or_5_out, or_6_out, or_7_out, or_8_out, or_9_out;

  not not_1 (not_1_out, i0);
  not not_2 (not_2_out, i1);
  not not_3 (not_3_out, i2);
  not not_4 (not_4_out, i3);
  and and_1 (and_1_out, COUNT, not_5_out);
  not not_5 (not_5_out, LOAD);
  and and_2 (and_2_out, i0, LOAD);
  and and_3 (and_3_out, not_1_out, LOAD);
  and and_4 (and_4_out, i1, LOAD);
  and and_5 (and_5_out, LOAD, not_2_out);
  and and_6 (and_6_out, i2, LOAD);
  and and_7 (and_7_out, not_3_out, LOAD);
  and and_8 (and_8_out, i3, LOAD);
  and and_9 (and_9_out, not_4_out, LOAD);
  and and_10 (and_10_out, q1, q2);
  and and_11 (and_11_out, q0, and_1_out);
  and and_12 (and_12_out, and_1_out, q0, q1);
  and and_13 (and_13_out, q2, q1, q0, and_1_out);
  or or_1 (or_1_out, and_10_out, CLEAR);
  or or_2 (or_2_out, and_2_out, and_1_out);
  or or_3 (or_3_out, and_3_out, and_1_out);
  or or_4 (or_4_out, and_4_out, and_11_out);
  or or_5 (or_5_out, and_11_out, and_5_out);
  or or_6 (or_6_out, and_6_out, and_12_out);
  or or_7 (or_7_out, and_12_out, and_7_out);
  or or_8 (or_8_out, and_8_out, and_13_out);
  or or_9 (or_9_out, and_13_out, and_9_out);
  J_K_Flip_Flop #(.trigger("falling")) j_k_ff_1 (
    .J(or_2_out), .clk(CLOCK), .K(or_3_out), .Q(q0), .reset(or_1_out));  // open: Qn, preset, en
  J_K_Flip_Flop #(.trigger("falling")) j_k_ff_2 (
    .J(or_4_out), .clk(CLOCK), .K(or_5_out), .Q(q1), .reset(or_1_out));  // open: Qn, preset, en
  J_K_Flip_Flop #(.trigger("falling")) j_k_ff_3 (
    .J(or_6_out), .clk(CLOCK), .K(or_7_out), .Q(q2), .reset(or_1_out));  // open: Qn, preset, en
  J_K_Flip_Flop #(.trigger("falling")) j_k_ff_4 (
    .J(or_8_out), .clk(CLOCK), .K(or_9_out), .Q(q3), .reset(or_1_out));  // open: Qn, preset, en

  // Notes on the sheet:
  //   MOD 6 COUNTER
  //   (with parallel loading)
endmodule

module clock (
  input  [3:0] in_1,
  input  [3:0] in_2,
  input  [3:0] in_3,
  input  [3:0] in_4,
  input  [3:0] in_5,
  input  [3:0] in_6,
  input  clock,
  input  clear,
  input  UP_COUNT,
  input  PARALLEL_LOAD,
  output [3:0] out_11,
  output [3:0] out_12,
  output [3:0] HH,
  output [3:0] out_14,
  output [3:0] MM,
  output [3:0] out_16
);

  wire and_1_out, and_2_out, and_3_out, and_4_out, multiplexer_1_out, multiplexer_2_out;

  mod_24 mod_24_1 (
    .CLOCK(multiplexer_1_out), .CLEAR(clear), .I3(in_4[3]), .I2(in_4[2]), .I1(in_4[1]), .I0(in_4[0]),
    .COUNT(UP_COUNT), .LOAD(PARALLEL_LOAD), .I1_2(in_6[1]), .I0_2(in_6[0]), .q0(out_14[0]), .q1(out_14[1]),
    .q2(out_14[2]), .q3(out_14[3]), .p0(HH[0]), .p1(HH[1]));
  Multiplexer #(.enable("false")) multiplexer_1 (
    .in0(and_1_out), .in1(clock), .out(multiplexer_1_out), .sel(PARALLEL_LOAD));
  and and_1 (and_1_out, multiplexer_2_out, MM[0], MM[2], 1'b1, and_2_out);
  mod_60 mod_60_1 (
    .CLOCK(multiplexer_2_out), .CLEAR(clear), .I3(in_2[3]), .I2(in_2[2]), .I1(in_2[1]), .I0(in_2[0]),
    .COUNT(UP_COUNT), .LOAD(PARALLEL_LOAD), .I2_2(in_5[2]), .I1_2(in_5[1]), .I0_2(in_5[0]), .q3(out_16[3]),
    .q2(out_16[2]), .q1(out_16[1]), .q0(out_16[0]), .p2(MM[2]), .p1(MM[1]), .p0(MM[0]));
  and and_2 (and_2_out, out_16[3], out_16[0]);
  Multiplexer #(.enable("false")) multiplexer_2 (
    .in0(and_3_out), .in1(clock), .out(multiplexer_2_out), .sel(PARALLEL_LOAD));
  and and_3 (and_3_out, out_11[0], out_11[2], clock, and_4_out, 1'b1);
  mod_60 mod_60_2 (
    .CLOCK(clock), .CLEAR(clear), .I3(in_3[3]), .I2(in_3[2]), .I1(in_3[1]), .I0(in_3[0]), .COUNT(UP_COUNT),
    .LOAD(PARALLEL_LOAD), .I2_2(in_1[2]), .I1_2(in_1[1]), .I0_2(in_1[0]), .q3(out_12[3]), .q2(out_12[2]),
    .q1(out_12[1]), .q0(out_12[0]), .p2(out_11[2]), .p1(out_11[1]), .p0(out_11[0]));
  and and_4 (and_4_out, out_12[3], out_12[0]);

  assign HH[3:2] = 2'b00;
  assign MM[3] = 1'b0;
  assign out_11[3] = 1'b0;

  // Notes on the sheet:
  //   CLOCK
  //   (with parallel loading)
  //   clock
  //   SS
endmodule

module mod_2 (
  input  clock,
  input  clear,
  output q0
);

  T_Flip_Flop #(.trigger("falling")) t_ff_1 (.clk(clock), .T(1'b1), .Q(q0), .reset(clear));  // open: Qn, preset, en
endmodule

module hours_combination (
  input  [3:0] decade,
  input  [3:0] mod_4,
  output out_3
);

  wire and_1_out, and_2_out, and_3_out, and_4_out, not_1_out, not_2_out, not_3_out, not_4_out, not_5_out;

  not not_1 (not_1_out, mod_4[0]);
  not not_2 (not_2_out, decade[0]);
  not not_3 (not_3_out, decade[1]);
  not not_4 (not_4_out, decade[2]);
  not not_5 (not_5_out, decade[3]);
  and and_1 (and_1_out, decade[2], decade[1], decade[0], mod_4[0]);
  and and_2 (and_2_out, mod_4[0], decade[3]);
  and and_3 (and_3_out, decade[0], not_1_out, decade[3]);
  and and_4 (and_4_out, not_2_out, not_3_out, not_4_out, not_5_out, mod_4[0]);
  or or_1 (out_3, and_3_out, and_4_out, and_1_out, and_2_out);

  // Notes on the sheet:
  //   busy hours combinatorial
endmodule

module timer60 (
  input  CLOCK,
  input  CLEAR,
  output clock_out,
  output [3:0] mod3,
  output [3:0] mod10
);

  mod_60 mod_60_1 (
    .CLOCK(CLOCK), .CLEAR(CLEAR), .COUNT(1'b1), .LOAD(1'b0), .q3(mod10[3]), .q2(mod10[2]), .q1(mod10[1]),
    .q0(mod10[0]), .p2(mod3[2]), .p1(mod3[1]), .p0(mod3[0]));  // open: I3, I2, I1, I0, I2_2, I1_2, I0_2
  and and_1 (clock_out, mod10[1], mod10[3], mod3[2], mod3[1]);

  assign mod3[3] = 1'b0;

  // Notes on the sheet:
  //   timing circuit for 60s
endmodule
